// Logisim project curcuit.circ as structural Verilog: 4 circuits, main circuit CPU
module CPU (
);

  wire ALU_calc, ALU_out, clock_1_out, clock_2_out, cpu_clock, HLT, instruction_decoder_1_ir_i,
       instruction_decoder_1_ir_o, jump, M_clock, not_1_out, num1_in, num1_out, num2_in, num2_out, or_1_out,
       PC_out, PC_up, R0_in, R0_out, R1_in, R1_out, R2_in, R2_out, RAM_adr_in, RAM_in, RAM_out, reset,
       reset_SBC;
  wire [2:0] alu_1_carry_out, bit_extender_5_out, CPU_flaga;
  wire [3:0] ALU_inst;
  wire [8:0] register_6_q_2;
  wire [15:0] bit_extender_1_out, bit_extender_3_out, programcounter_1_ip, programcounter_2_ip, register_1_q;
  wire [22:0] register_6_q;
  wire [31:0] alu_1_num_out, ALU_out_q, bit_extender_2_out, bit_extender_4_out, multiplexer_1_out, num2_q,
       ram_1_dout, register_2_q, register_3_q, register_4_q, register_5_q;

  LedBar #(.matrixcols(32)) ledbar_1 (
    .led0(bit_extender_2_out[31]), .led1(bit_extender_2_out[30]), .led2(bit_extender_2_out[29]),
    .led3(bit_extender_2_out[28]), .led4(bit_extender_2_out[27]), .led5(bit_extender_2_out[26]),
    .led6(bit_extender_2_out[25]), .led7(bit_extender_2_out[24]), .led8(bit_extender_2_out[23]),
    .led9(bit_extender_2_out[22]), .led10(bit_extender_2_out[21]), .led11(bit_extender_2_out[20]),
    .led12(bit_extender_2_out[19]), .led13(bit_extender_2_out[18]), .led14(bit_extender_2_out[17]),
    .led15(bit_extender_2_out[16]), .led16(bit_extender_2_out[15]), .led17(bit_extender_2_out[14]),
    .led18(bit_extender_2_out[13]), .led19(bit_extender_2_out[12]), .led20(bit_extender_2_out[11]),
    .led21(bit_extender_2_out[10]), .led22(bit_extender_2_out[9]), .led23(bit_extender_2_out[8]),
    .led24(bit_extender_2_out[7]), .led25(bit_extender_2_out[6]), .led26(bit_extender_2_out[5]),
    .led27(bit_extender_2_out[4]), .led28(bit_extender_2_out[3]), .led29(bit_extender_2_out[2]),
    .led30(bit_extender_2_out[1]), .led31(bit_extender_2_out[0]));
  LedBar #(.matrixcols(32)) ledbar_2 (
    .led0(multiplexer_1_out[0]), .led1(multiplexer_1_out[1]), .led2(multiplexer_1_out[2]),
    .led3(multiplexer_1_out[3]), .led4(multiplexer_1_out[4]), .led5(multiplexer_1_out[5]),
    .led6(multiplexer_1_out[6]), .led7(multiplexer_1_out[7]), .led8(multiplexer_1_out[8]),
    .led9(multiplexer_1_out[9]), .led10(multiplexer_1_out[10]), .led11(multiplexer_1_out[11]),
    .led12(multiplexer_1_out[12]), .led13(multiplexer_1_out[13]), .led14(multiplexer_1_out[14]),
    .led15(multiplexer_1_out[15]), .led16(multiplexer_1_out[16]), .led17(multiplexer_1_out[17]),
    .led18(multiplexer_1_out[18]), .led19(multiplexer_1_out[19]), .led20(multiplexer_1_out[20]),
    .led21(multiplexer_1_out[21]), .led22(multiplexer_1_out[22]), .led23(multiplexer_1_out[23]),
    .led24(multiplexer_1_out[24]), .led25(multiplexer_1_out[25]), .led26(multiplexer_1_out[26]),
    .led27(multiplexer_1_out[27]), .led28(multiplexer_1_out[28]), .led29(multiplexer_1_out[29]),
    .led30(multiplexer_1_out[30]), .led31(multiplexer_1_out[31]));
  LedBar #(.matrixcols(32)) ledbar_3 (
    .led0(register_2_q[31]), .led1(register_2_q[30]), .led2(register_2_q[29]), .led3(register_2_q[28]),
    .led4(register_2_q[27]), .led5(register_2_q[26]), .led6(register_2_q[25]), .led7(register_2_q[24]),
    .led8(register_2_q[23]), .led9(register_2_q[22]), .led10(register_2_q[21]), .led11(register_2_q[20]),
    .led12(register_2_q[19]), .led13(register_2_q[18]), .led14(register_2_q[17]), .led15(register_2_q[16]),
    .led16(register_2_q[15]), .led17(register_2_q[14]), .led18(register_2_q[13]), .led19(register_2_q[12]),
    .led20(register_2_q[11]), .led21(register_2_q[10]), .led22(register_2_q[9]), .led23(register_2_q[8]),
    .led24(register_2_q[7]), .led25(register_2_q[6]), .led26(register_2_q[5]), .led27(register_2_q[4]),
    .led28(register_2_q[3]), .led29(register_2_q[2]), .led30(register_2_q[1]), .led31(register_2_q[0]));
  LedBar #(.matrixcols(32)) ledbar_4 (
    .led0(num2_q[31]), .led1(num2_q[30]), .led2(num2_q[29]), .led3(num2_q[28]), .led4(num2_q[27]),
    .led5(num2_q[26]), .led6(num2_q[25]), .led7(num2_q[24]), .led8(num2_q[23]), .led9(num2_q[22]),
    .led10(num2_q[21]), .led11(num2_q[20]), .led12(num2_q[19]), .led13(num2_q[18]), .led14(num2_q[17]),
    .led15(num2_q[16]), .led16(num2_q[15]), .led17(num2_q[14]), .led18(num2_q[13]), .led19(num2_q[12]),
    .led20(num2_q[11]), .led21(num2_q[10]), .led22(num2_q[9]), .led23(num2_q[8]), .led24(num2_q[7]),
    .led25(num2_q[6]), .led26(num2_q[5]), .led27(num2_q[4]), .led28(num2_q[3]), .led29(num2_q[2]),
    .led30(num2_q[1]), .led31(num2_q[0]));
  LedBar #(.matrixcols(32)) ledbar_5 (
    .led0(ALU_out_q[31]), .led1(ALU_out_q[30]), .led2(ALU_out_q[29]), .led3(ALU_out_q[28]),
    .led4(ALU_out_q[27]), .led5(ALU_out_q[26]), .led6(ALU_out_q[25]), .led7(ALU_out_q[24]),
    .led8(ALU_out_q[23]), .led9(ALU_out_q[22]), .led10(ALU_out_q[21]), .led11(ALU_out_q[20]),
    .led12(ALU_out_q[19]), .led13(ALU_out_q[18]), .led14(ALU_out_q[17]), .led15(ALU_out_q[16]),
    .led16(ALU_out_q[15]), .led17(ALU_out_q[14]), .led18(ALU_out_q[13]), .led19(ALU_out_q[12]),
    .led20(ALU_out_q[11]), .led21(ALU_out_q[10]), .led22(ALU_out_q[9]), .led23(ALU_out_q[8]),
    .led24(ALU_out_q[7]), .led25(ALU_out_q[6]), .led26(ALU_out_q[5]), .led27(ALU_out_q[4]),
    .led28(ALU_out_q[3]), .led29(ALU_out_q[2]), .led30(ALU_out_q[1]), .led31(ALU_out_q[0]));
  LedBar #(.matrixcols(32)) ledbar_6 (
    .led0(register_6_q[0]), .led1(register_6_q[1]), .led2(register_6_q[2]), .led3(register_6_q[3]),
    .led4(register_6_q[4]), .led5(register_6_q[5]), .led6(register_6_q[6]), .led7(register_6_q[7]),
    .led8(register_6_q[8]), .led9(register_6_q[9]), .led10(register_6_q[10]), .led11(register_6_q[11]),
    .led12(register_6_q[12]), .led13(register_6_q[13]), .led14(register_6_q[14]), .led15(register_6_q[15]),
    .led16(register_6_q[16]), .led17(register_6_q[17]), .led18(register_6_q[18]), .led19(register_6_q[19]),
    .led20(register_6_q[20]), .led21(register_6_q[21]), .led22(register_6_q[22]), .led23(register_6_q_2[0]),
    .led24(register_6_q_2[1]), .led25(register_6_q_2[2]), .led26(register_6_q_2[3]),
    .led27(register_6_q_2[4]), .led28(register_6_q_2[5]), .led29(register_6_q_2[6]),
    .led30(register_6_q_2[7]), .led31(register_6_q_2[8]));
  LedBar #(.matrixcols(32)) ledbar_7 (
    .led0(register_3_q[31]), .led1(register_3_q[30]), .led2(register_3_q[29]), .led3(register_3_q[28]),
    .led4(register_3_q[27]), .led5(register_3_q[26]), .led6(register_3_q[25]), .led7(register_3_q[24]),
    .led8(register_3_q[23]), .led9(register_3_q[22]), .led10(register_3_q[21]), .led11(register_3_q[20]),
    .led12(register_3_q[19]), .led13(register_3_q[18]), .led14(register_3_q[17]), .led15(register_3_q[16]),
    .led16(register_3_q[15]), .led17(register_3_q[14]), .led18(register_3_q[13]), .led19(register_3_q[12]),
    .led20(register_3_q[11]), .led21(register_3_q[10]), .led22(register_3_q[9]), .led23(register_3_q[8]),
    .led24(register_3_q[7]), .led25(register_3_q[6]), .led26(register_3_q[5]), .led27(register_3_q[4]),
    .led28(register_3_q[3]), .led29(register_3_q[2]), .led30(register_3_q[1]), .led31(register_3_q[0]));
  LedBar #(.matrixcols(32)) ledbar_8 (
    .led0(register_4_q[31]), .led1(register_4_q[30]), .led2(register_4_q[29]), .led3(register_4_q[28]),
    .led4(register_4_q[27]), .led5(register_4_q[26]), .led6(register_4_q[25]), .led7(register_4_q[24]),
    .led8(register_4_q[23]), .led9(register_4_q[22]), .led10(register_4_q[21]), .led11(register_4_q[20]),
    .led12(register_4_q[19]), .led13(register_4_q[18]), .led14(register_4_q[17]), .led15(register_4_q[16]),
    .led16(register_4_q[15]), .led17(register_4_q[14]), .led18(register_4_q[13]), .led19(register_4_q[12]),
    .led20(register_4_q[11]), .led21(register_4_q[10]), .led22(register_4_q[9]), .led23(register_4_q[8]),
    .led24(register_4_q[7]), .led25(register_4_q[6]), .led26(register_4_q[5]), .led27(register_4_q[4]),
    .led28(register_4_q[3]), .led29(register_4_q[2]), .led30(register_4_q[1]), .led31(register_4_q[0]));
  LedBar #(.matrixcols(32)) ledbar_9 (
    .led0(register_5_q[31]), .led1(register_5_q[30]), .led2(register_5_q[29]), .led3(register_5_q[28]),
    .led4(register_5_q[27]), .led5(register_5_q[26]), .led6(register_5_q[25]), .led7(register_5_q[24]),
    .led8(register_5_q[23]), .led9(register_5_q[22]), .led10(register_5_q[21]), .led11(register_5_q[20]),
    .led12(register_5_q[19]), .led13(register_5_q[18]), .led14(register_5_q[17]), .led15(register_5_q[16]),
    .led16(register_5_q[15]), .led17(register_5_q[14]), .led18(register_5_q[13]), .led19(register_5_q[12]),
    .led20(register_5_q[11]), .led21(register_5_q[10]), .led22(register_5_q[9]), .led23(register_5_q[8]),
    .led24(register_5_q[7]), .led25(register_5_q[6]), .led26(register_5_q[5]), .led27(register_5_q[4]),
    .led28(register_5_q[3]), .led29(register_5_q[2]), .led30(register_5_q[1]), .led31(register_5_q[0]));
  Register #(.width(16)) register_1 (
    .D(bit_extender_3_out), .en(RAM_adr_in), .clk(cpu_clock), .Q(register_1_q), .clr(reset));
  RAM #(.addrWidth(16), .dataWidth(32)) ram_1 (
    .addr(register_1_q), .we(RAM_in), .oe(RAM_out), .clk(M_clock), .din(multiplexer_1_out), .dout(ram_1_dout));
  Bit_Extender #(.in_width(32), .\type ("zero")) bit_extender_1 (
    .in({multiplexer_1_out[0], multiplexer_1_out[1], multiplexer_1_out[2], multiplexer_1_out[3], multiplexer_1_out[4], multiplexer_1_out[5], multiplexer_1_out[6], multiplexer_1_out[7], multiplexer_1_out[8], multiplexer_1_out[9], multiplexer_1_out[10], multiplexer_1_out[11], multiplexer_1_out[12], multiplexer_1_out[13], multiplexer_1_out[14], multiplexer_1_out[15], multiplexer_1_out[16], multiplexer_1_out[17], multiplexer_1_out[18], multiplexer_1_out[19], multiplexer_1_out[20], multiplexer_1_out[21], multiplexer_1_out[22], multiplexer_1_out[23], multiplexer_1_out[24], multiplexer_1_out[25], multiplexer_1_out[26], multiplexer_1_out[27], multiplexer_1_out[28], multiplexer_1_out[29], multiplexer_1_out[30], multiplexer_1_out[31]}),
    .out(bit_extender_1_out));
  ProgramCounter programcounter_1 (
    .JmpAddr(bit_extender_1_out), .Reset(reset), .Jmp(jump), .Clock(PC_up), .ip(programcounter_1_ip));
  assign bit_extender_2_out = {{16{programcounter_1_ip[15]}}, programcounter_1_ip};  // Bit_Extender bit_extender_2
  Bit_Extender #(.in_width(32), .\type ("zero")) bit_extender_3 (
    .in({multiplexer_1_out[0], multiplexer_1_out[1], multiplexer_1_out[2], multiplexer_1_out[3], multiplexer_1_out[4], multiplexer_1_out[5], multiplexer_1_out[6], multiplexer_1_out[7], multiplexer_1_out[8], multiplexer_1_out[9], multiplexer_1_out[10], multiplexer_1_out[11], multiplexer_1_out[12], multiplexer_1_out[13], multiplexer_1_out[14], multiplexer_1_out[15], multiplexer_1_out[16], multiplexer_1_out[17], multiplexer_1_out[18], multiplexer_1_out[19], multiplexer_1_out[20], multiplexer_1_out[21], multiplexer_1_out[22], multiplexer_1_out[23], multiplexer_1_out[24], multiplexer_1_out[25], multiplexer_1_out[26], multiplexer_1_out[27], multiplexer_1_out[28], multiplexer_1_out[29], multiplexer_1_out[30], multiplexer_1_out[31]}),
    .out(bit_extender_3_out));
  Multiplexer #(.width(32)) multiplexer_1 (.in1(ram_1_dout), .out(multiplexer_1_out), .sel(RAM_out));  // open: in0
  Multiplexer #(.width(32)) multiplexer_2 (
    .in1(bit_extender_2_out),
    .out({multiplexer_1_out[0], multiplexer_1_out[1], multiplexer_1_out[2], multiplexer_1_out[3], multiplexer_1_out[4], multiplexer_1_out[5], multiplexer_1_out[6], multiplexer_1_out[7], multiplexer_1_out[8], multiplexer_1_out[9], multiplexer_1_out[10], multiplexer_1_out[11], multiplexer_1_out[12], multiplexer_1_out[13], multiplexer_1_out[14], multiplexer_1_out[15], multiplexer_1_out[16], multiplexer_1_out[17], multiplexer_1_out[18], multiplexer_1_out[19], multiplexer_1_out[20], multiplexer_1_out[21], multiplexer_1_out[22], multiplexer_1_out[23], multiplexer_1_out[24], multiplexer_1_out[25], multiplexer_1_out[26], multiplexer_1_out[27], multiplexer_1_out[28], multiplexer_1_out[29], multiplexer_1_out[30], multiplexer_1_out[31]}),
    .sel(PC_out));  // open: in0
  Multiplexer #(.width(32)) multiplexer_3 (
    .in1(register_2_q),
    .out({multiplexer_1_out[0], multiplexer_1_out[1], multiplexer_1_out[2], multiplexer_1_out[3], multiplexer_1_out[4], multiplexer_1_out[5], multiplexer_1_out[6], multiplexer_1_out[7], multiplexer_1_out[8], multiplexer_1_out[9], multiplexer_1_out[10], multiplexer_1_out[11], multiplexer_1_out[12], multiplexer_1_out[13], multiplexer_1_out[14], multiplexer_1_out[15], multiplexer_1_out[16], multiplexer_1_out[17], multiplexer_1_out[18], multiplexer_1_out[19], multiplexer_1_out[20], multiplexer_1_out[21], multiplexer_1_out[22], multiplexer_1_out[23], multiplexer_1_out[24], multiplexer_1_out[25], multiplexer_1_out[26], multiplexer_1_out[27], multiplexer_1_out[28], multiplexer_1_out[29], multiplexer_1_out[30], multiplexer_1_out[31]}),
    .sel(num1_out));  // open: in0
  Multiplexer #(.width(32)) multiplexer_4 (
    .in1(register_3_q),
    .out({multiplexer_1_out[0], multiplexer_1_out[1], multiplexer_1_out[2], multiplexer_1_out[3], multiplexer_1_out[4], multiplexer_1_out[5], multiplexer_1_out[6], multiplexer_1_out[7], multiplexer_1_out[8], multiplexer_1_out[9], multiplexer_1_out[10], multiplexer_1_out[11], multiplexer_1_out[12], multiplexer_1_out[13], multiplexer_1_out[14], multiplexer_1_out[15], multiplexer_1_out[16], multiplexer_1_out[17], multiplexer_1_out[18], multiplexer_1_out[19], multiplexer_1_out[20], multiplexer_1_out[21], multiplexer_1_out[22], multiplexer_1_out[23], multiplexer_1_out[24], multiplexer_1_out[25], multiplexer_1_out[26], multiplexer_1_out[27], multiplexer_1_out[28], multiplexer_1_out[29], multiplexer_1_out[30], multiplexer_1_out[31]}),
    .sel(R0_out));  // open: in0
  Multiplexer #(.width(32)) multiplexer_5 (
    .in1(register_4_q),
    .out({multiplexer_1_out[0], multiplexer_1_out[1], multiplexer_1_out[2], multiplexer_1_out[3], multiplexer_1_out[4], multiplexer_1_out[5], multiplexer_1_out[6], multiplexer_1_out[7], multiplexer_1_out[8], multiplexer_1_out[9], multiplexer_1_out[10], multiplexer_1_out[11], multiplexer_1_out[12], multiplexer_1_out[13], multiplexer_1_out[14], multiplexer_1_out[15], multiplexer_1_out[16], multiplexer_1_out[17], multiplexer_1_out[18], multiplexer_1_out[19], multiplexer_1_out[20], multiplexer_1_out[21], multiplexer_1_out[22], multiplexer_1_out[23], multiplexer_1_out[24], multiplexer_1_out[25], multiplexer_1_out[26], multiplexer_1_out[27], multiplexer_1_out[28], multiplexer_1_out[29], multiplexer_1_out[30], multiplexer_1_out[31]}),
    .sel(R1_out));  // open: in0
  Multiplexer #(.width(32)) multiplexer_6 (
    .in1(register_5_q),
    .out({multiplexer_1_out[0], multiplexer_1_out[1], multiplexer_1_out[2], multiplexer_1_out[3], multiplexer_1_out[4], multiplexer_1_out[5], multiplexer_1_out[6], multiplexer_1_out[7], multiplexer_1_out[8], multiplexer_1_out[9], multiplexer_1_out[10], multiplexer_1_out[11], multiplexer_1_out[12], multiplexer_1_out[13], multiplexer_1_out[14], multiplexer_1_out[15], multiplexer_1_out[16], multiplexer_1_out[17], multiplexer_1_out[18], multiplexer_1_out[19], multiplexer_1_out[20], multiplexer_1_out[21], multiplexer_1_out[22], multiplexer_1_out[23], multiplexer_1_out[24], multiplexer_1_out[25], multiplexer_1_out[26], multiplexer_1_out[27], multiplexer_1_out[28], multiplexer_1_out[29], multiplexer_1_out[30], multiplexer_1_out[31]}),
    .sel(R2_out));  // open: in0
  Register #(.width(32)) register_2 (
    .D({multiplexer_1_out[0], multiplexer_1_out[1], multiplexer_1_out[2], multiplexer_1_out[3], multiplexer_1_out[4], multiplexer_1_out[5], multiplexer_1_out[6], multiplexer_1_out[7], multiplexer_1_out[8], multiplexer_1_out[9], multiplexer_1_out[10], multiplexer_1_out[11], multiplexer_1_out[12], multiplexer_1_out[13], multiplexer_1_out[14], multiplexer_1_out[15], multiplexer_1_out[16], multiplexer_1_out[17], multiplexer_1_out[18], multiplexer_1_out[19], multiplexer_1_out[20], multiplexer_1_out[21], multiplexer_1_out[22], multiplexer_1_out[23], multiplexer_1_out[24], multiplexer_1_out[25], multiplexer_1_out[26], multiplexer_1_out[27], multiplexer_1_out[28], multiplexer_1_out[29], multiplexer_1_out[30], multiplexer_1_out[31]}),
    .en(num1_in), .clk(cpu_clock), .Q(register_2_q), .clr(reset));
  Multiplexer #(.width(32)) multiplexer_7 (
    .in1(num2_q),
    .out({multiplexer_1_out[0], multiplexer_1_out[1], multiplexer_1_out[2], multiplexer_1_out[3], multiplexer_1_out[4], multiplexer_1_out[5], multiplexer_1_out[6], multiplexer_1_out[7], multiplexer_1_out[8], multiplexer_1_out[9], multiplexer_1_out[10], multiplexer_1_out[11], multiplexer_1_out[12], multiplexer_1_out[13], multiplexer_1_out[14], multiplexer_1_out[15], multiplexer_1_out[16], multiplexer_1_out[17], multiplexer_1_out[18], multiplexer_1_out[19], multiplexer_1_out[20], multiplexer_1_out[21], multiplexer_1_out[22], multiplexer_1_out[23], multiplexer_1_out[24], multiplexer_1_out[25], multiplexer_1_out[26], multiplexer_1_out[27], multiplexer_1_out[28], multiplexer_1_out[29], multiplexer_1_out[30], multiplexer_1_out[31]}),
    .sel(num2_out));  // open: in0
  Register #(.width(32)) num2 (
    .D({multiplexer_1_out[0], multiplexer_1_out[1], multiplexer_1_out[2], multiplexer_1_out[3], multiplexer_1_out[4], multiplexer_1_out[5], multiplexer_1_out[6], multiplexer_1_out[7], multiplexer_1_out[8], multiplexer_1_out[9], multiplexer_1_out[10], multiplexer_1_out[11], multiplexer_1_out[12], multiplexer_1_out[13], multiplexer_1_out[14], multiplexer_1_out[15], multiplexer_1_out[16], multiplexer_1_out[17], multiplexer_1_out[18], multiplexer_1_out[19], multiplexer_1_out[20], multiplexer_1_out[21], multiplexer_1_out[22], multiplexer_1_out[23], multiplexer_1_out[24], multiplexer_1_out[25], multiplexer_1_out[26], multiplexer_1_out[27], multiplexer_1_out[28], multiplexer_1_out[29], multiplexer_1_out[30], multiplexer_1_out[31]}),
    .en(num2_in), .clk(cpu_clock), .Q(num2_q), .clr(reset));
  Register #(.width(32)) register_3 (
    .D({multiplexer_1_out[0], multiplexer_1_out[1], multiplexer_1_out[2], multiplexer_1_out[3], multiplexer_1_out[4], multiplexer_1_out[5], multiplexer_1_out[6], multiplexer_1_out[7], multiplexer_1_out[8], multiplexer_1_out[9], multiplexer_1_out[10], multiplexer_1_out[11], multiplexer_1_out[12], multiplexer_1_out[13], multiplexer_1_out[14], multiplexer_1_out[15], multiplexer_1_out[16], multiplexer_1_out[17], multiplexer_1_out[18], multiplexer_1_out[19], multiplexer_1_out[20], multiplexer_1_out[21], multiplexer_1_out[22], multiplexer_1_out[23], multiplexer_1_out[24], multiplexer_1_out[25], multiplexer_1_out[26], multiplexer_1_out[27], multiplexer_1_out[28], multiplexer_1_out[29], multiplexer_1_out[30], multiplexer_1_out[31]}),
    .en(R0_in), .clk(cpu_clock), .Q(register_3_q), .clr(reset));
  Register #(.width(32)) register_4 (
    .D({multiplexer_1_out[0], multiplexer_1_out[1], multiplexer_1_out[2], multiplexer_1_out[3], multiplexer_1_out[4], multiplexer_1_out[5], multiplexer_1_out[6], multiplexer_1_out[7], multiplexer_1_out[8], multiplexer_1_out[9], multiplexer_1_out[10], multiplexer_1_out[11], multiplexer_1_out[12], multiplexer_1_out[13], multiplexer_1_out[14], multiplexer_1_out[15], multiplexer_1_out[16], multiplexer_1_out[17], multiplexer_1_out[18], multiplexer_1_out[19], multiplexer_1_out[20], multiplexer_1_out[21], multiplexer_1_out[22], multiplexer_1_out[23], multiplexer_1_out[24], multiplexer_1_out[25], multiplexer_1_out[26], multiplexer_1_out[27], multiplexer_1_out[28], multiplexer_1_out[29], multiplexer_1_out[30], multiplexer_1_out[31]}),
    .en(R1_in), .clk(cpu_clock), .Q(register_4_q), .clr(reset));
  Register #(.width(32)) register_5 (
    .D({multiplexer_1_out[0], multiplexer_1_out[1], multiplexer_1_out[2], multiplexer_1_out[3], multiplexer_1_out[4], multiplexer_1_out[5], multiplexer_1_out[6], multiplexer_1_out[7], multiplexer_1_out[8], multiplexer_1_out[9], multiplexer_1_out[10], multiplexer_1_out[11], multiplexer_1_out[12], multiplexer_1_out[13], multiplexer_1_out[14], multiplexer_1_out[15], multiplexer_1_out[16], multiplexer_1_out[17], multiplexer_1_out[18], multiplexer_1_out[19], multiplexer_1_out[20], multiplexer_1_out[21], multiplexer_1_out[22], multiplexer_1_out[23], multiplexer_1_out[24], multiplexer_1_out[25], multiplexer_1_out[26], multiplexer_1_out[27], multiplexer_1_out[28], multiplexer_1_out[29], multiplexer_1_out[30], multiplexer_1_out[31]}),
    .en(R2_in), .clk(cpu_clock), .Q(register_5_q), .clr(reset));
  Multiplexer #(.width(32)) multiplexer_8 (
    .in1(bit_extender_4_out),
    .out({multiplexer_1_out[0], multiplexer_1_out[1], multiplexer_1_out[2], multiplexer_1_out[3], multiplexer_1_out[4], multiplexer_1_out[5], multiplexer_1_out[6], multiplexer_1_out[7], multiplexer_1_out[8], multiplexer_1_out[9], multiplexer_1_out[10], multiplexer_1_out[11], multiplexer_1_out[12], multiplexer_1_out[13], multiplexer_1_out[14], multiplexer_1_out[15], multiplexer_1_out[16], multiplexer_1_out[17], multiplexer_1_out[18], multiplexer_1_out[19], multiplexer_1_out[20], multiplexer_1_out[21], multiplexer_1_out[22], multiplexer_1_out[23], multiplexer_1_out[24], multiplexer_1_out[25], multiplexer_1_out[26], multiplexer_1_out[27], multiplexer_1_out[28], multiplexer_1_out[29], multiplexer_1_out[30], multiplexer_1_out[31]}),
    .sel(instruction_decoder_1_ir_o));  // open: in0
  Clock clock_1 (.out(clock_1_out));
  Register #(.width(32)) register_6 (
    .D({multiplexer_1_out[0], multiplexer_1_out[1], multiplexer_1_out[2], multiplexer_1_out[3], multiplexer_1_out[4], multiplexer_1_out[5], multiplexer_1_out[6], multiplexer_1_out[7], multiplexer_1_out[8], multiplexer_1_out[9], multiplexer_1_out[10], multiplexer_1_out[11], multiplexer_1_out[12], multiplexer_1_out[13], multiplexer_1_out[14], multiplexer_1_out[15], multiplexer_1_out[16], multiplexer_1_out[17], multiplexer_1_out[18], multiplexer_1_out[19], multiplexer_1_out[20], multiplexer_1_out[21], multiplexer_1_out[22], multiplexer_1_out[23], multiplexer_1_out[24], multiplexer_1_out[25], multiplexer_1_out[26], multiplexer_1_out[27], multiplexer_1_out[28], multiplexer_1_out[29], multiplexer_1_out[30], multiplexer_1_out[31]}),
    .en(instruction_decoder_1_ir_i), .clk(cpu_clock),
    .Q({register_6_q[0], register_6_q[1], register_6_q[2], register_6_q[3], register_6_q[4], register_6_q[5], register_6_q[6], register_6_q[7], register_6_q[8], register_6_q[9], register_6_q[10], register_6_q[11], register_6_q[12], register_6_q[13], register_6_q[14], register_6_q[15], register_6_q[16], register_6_q[17], register_6_q[18], register_6_q[19], register_6_q[20], register_6_q[21], register_6_q[22], register_6_q_2[0], register_6_q_2[1], register_6_q_2[2], register_6_q_2[3], register_6_q_2[4], register_6_q_2[5], register_6_q_2[6], register_6_q_2[7], register_6_q_2[8]}),
    .clr(reset));
  Button button_1 (.out(reset));
  Clock #(.highDuration(2), .lowDuration(2)) clock_2 (.out(clock_2_out));
  not not_1 (not_1_out, HLT);
  ALU alu_1 (
    .instruction(ALU_inst), .num1(register_2_q), .num2(num2_q), .borrow_in(1'b0), .carry_in(1'b0),
    .mul_carry_in({32{1'b0}}), .div_upper({32{1'b0}}), .carry_out(alu_1_carry_out[0]),
    .borrow_out(alu_1_carry_out[1]), .comp_out(alu_1_carry_out[2]), .num_out(alu_1_num_out));
  assign bit_extender_4_out = {{9{1'b0}}, register_6_q};  // Bit_Extender bit_extender_4
  and and_1 (cpu_clock, clock_2_out, not_1_out);
  and and_2 (M_clock, not_1_out, clock_1_out);
  Register #(.width(3)) register_7 (.D(alu_1_carry_out), .en(ALU_calc), .clk(cpu_clock), .Q(CPU_flaga), .clr(reset));
  Multiplexer #(.width(32)) multiplexer_9 (
    .in1(ALU_out_q),
    .out({multiplexer_1_out[0], multiplexer_1_out[1], multiplexer_1_out[2], multiplexer_1_out[3], multiplexer_1_out[4], multiplexer_1_out[5], multiplexer_1_out[6], multiplexer_1_out[7], multiplexer_1_out[8], multiplexer_1_out[9], multiplexer_1_out[10], multiplexer_1_out[11], multiplexer_1_out[12], multiplexer_1_out[13], multiplexer_1_out[14], multiplexer_1_out[15], multiplexer_1_out[16], multiplexer_1_out[17], multiplexer_1_out[18], multiplexer_1_out[19], multiplexer_1_out[20], multiplexer_1_out[21], multiplexer_1_out[22], multiplexer_1_out[23], multiplexer_1_out[24], multiplexer_1_out[25], multiplexer_1_out[26], multiplexer_1_out[27], multiplexer_1_out[28], multiplexer_1_out[29], multiplexer_1_out[30], multiplexer_1_out[31]}),
    .sel(ALU_out));  // open: in0
  Register #(.width(32)) u_ALU_out (.D(alu_1_num_out), .en(ALU_calc), .clk(cpu_clock), .Q(ALU_out_q), .clr(reset));
  or or_1 (or_1_out, reset_SBC, reset);
  instruction_decoder instruction_decoder_1 (
    .instruction(register_6_q_2), .sub_stage(bit_extender_5_out), .carry(CPU_flaga[0]),
    .barrow(CPU_flaga[1]), .comp(CPU_flaga[2]), .RSC(reset_SBC), .MA_In(RAM_adr_in), .M_I(RAM_in),
    .M_O(RAM_out), .IR_I(instruction_decoder_1_ir_i), .IR_O(instruction_decoder_1_ir_o), .PC_O(PC_out),
    .PC_Up(PC_up), .PC_jmp(jump), .ALU_inst(ALU_inst), .A_I(ALU_calc), .A_O(ALU_out), .N1_I(num1_in),
    .N1_O(num1_out), .N2_I(num2_in), .N2_O(num2_out), .R0I(R0_in), .R0O(R0_out), .R1I(R1_in), .R1O(R1_out),
    .R2I(R2_in), .R2O(R2_out), .HLT(HLT));
  ProgramCounter programcounter_2 (
    .JmpAddr({16{1'b0}}), .Reset(or_1_out), .Jmp(1'b0), .Clock(cpu_clock), .ip(programcounter_2_ip));
  LedBar #(.matrixcols(3)) ledbar_10 (
    .led0(bit_extender_5_out[2]), .led1(bit_extender_5_out[1]), .led2(bit_extender_5_out[0]));
  Bit_Extender #(.in_width(16), .out_width(3)) bit_extender_5 (.in(programcounter_2_ip), .out(bit_extender_5_out));

  // Notes on the sheet:
  //   Program Counter
  //   BUS
  //   RN1
  //   RN2
  //   RA
  //   IR
  //   R0
  //   R1
  //   R2
endmodule

module ProgramCounter (
  input  [15:0] JmpAddr,
  input  Reset,
  input  Jmp,
  input  Clock,
  output [15:0] ip
);

  wire [15:0] adder_1_out, multiplexer_1_out;

  Adder #(.width(16)) adder_1 (.a(ip), .b(16'h1), .out(adder_1_out));  // open: cin, cout
  Multiplexer #(.width(16)) multiplexer_1 (.in0(adder_1_out), .in1(JmpAddr), .out(multiplexer_1_out), .sel(Jmp));
  Register #(.width(16)) register_1 (.D(multiplexer_1_out), .en(1'b1), .Q(ip), .clk(Clock), .clr(Reset));
endmodule

module ALU (
  input  [3:0] instruction,
  input  [31:0] num1,
  input  [31:0] num2,
  input  borrow_in,
  input  carry_in,
  input  [31:0] mul_carry_in,
  input  [31:0] div_upper,
  output carry_out,
  output borrow_out,
  output comp_out,
  output [31:0] num_out
);

  wire comparator_1_eq, comparator_1_gt, comparator_1_lt, comparator_2_eq, comparator_2_gt, comparator_2_lt,
       fpcomparator_1_p3, fpcomparator_1_p4, fpcomparator_1_p5;
  wire [31:0] adder_1_out, divider_1_out, divider_2_out, fpadder_1_out, fpdivider_1_out, fpmultiplier_1_out,
       fpnegator_1_p2, fpsubtractor_1_out, fptoint_1_p2, inttofp_1_p2, inttofp_2_p2, multiplier_1_out,
       multiplier_2_out, negator_1_out, subtractor_1_out;

  Adder #(.width(32)) adder_1 (.a(num2), .b(num1), .out(adder_1_out), .cin(carry_in), .cout(carry_out));
  Subtractor #(.width(32)) subtractor_1 (
    .a(num2), .b(num1), .out(subtractor_1_out), .bin(borrow_in), .bout(borrow_out));
  Multiplier #(.width(32)) multiplier_1 (.a(num2), .b(num1), .out(multiplier_1_out), .cin(mul_carry_in));  // open: cout
  Multiplier #(.mode("twosComplement"), .width(32)) multiplier_2 (
    .a(num2), .b(num1), .out(multiplier_2_out), .cin(mul_carry_in));  // open: cout
  Divider #(.width(32)) divider_1 (.a(num2), .b(num1), .out(divider_1_out), .upper(div_upper));  // open: rem
  Divider #(.mode("twosComplement"), .width(32)) divider_2 (
    .a(num2), .b(num1), .out(divider_2_out), .upper(div_upper));  // open: rem
  Negator #(.width(32)) negator_1 (.in(num1), .out(negator_1_out));
  // IntToFP #(.mode("unsigned"), .width(32)) inttofp_1: pin names not known; wires that end beside it: num1, inttofp_1_p2
  // IntToFP #(.width(32)) inttofp_2: pin names not known; wires that end beside it: num1, inttofp_2_p2
  // FPToInt #(.width(32)) fptoint_1: pin names not known; wires that end beside it: num1, fptoint_1_p2
  Comparator #(.mode("unsigned"), .width(32)) comparator_1 (
    .a(num2), .b(num1), .gt(comparator_1_gt), .eq(comparator_1_eq), .lt(comparator_1_lt));
  Comparator #(.width(32)) comparator_2 (
    .a(num2), .b(num1), .gt(comparator_2_gt), .eq(comparator_2_eq), .lt(comparator_2_lt));
  // FPComparator fpcomparator_1: pin names not known; wires that end beside it: num2, num1, fpcomparator_1_p3, fpcomparator_1_p4, fpcomparator_1_p5
  FPAdder fpadder_1 (.a(num2), .b(num1), .out(fpadder_1_out));
  FPSubtractor fpsubtractor_1 (.a(num2), .b(num1), .out(fpsubtractor_1_out));
  FPMultiplier fpmultiplier_1 (.a(num1), .b(num1), .out(fpmultiplier_1_out));
  FPDivider fpdivider_1 (.a(num2), .b(num1), .out(fpdivider_1_out));
  // FPNegator fpnegator_1: pin names not known; wires that end beside it: num1, fpnegator_1_p2
  Multiplexer #(.select(4), .width(32)) multiplexer_1 (
    .in0(adder_1_out), .in1(subtractor_1_out), .in2(multiplier_1_out), .in3(multiplier_2_out),
    .in4(divider_1_out), .in5(divider_2_out), .in6(negator_1_out), .in7(fpadder_1_out),
    .in8(fpsubtractor_1_out), .in9(fpmultiplier_1_out), .in10(fpdivider_1_out), .in11(fpnegator_1_p2),
    .in12(inttofp_1_p2), .in13(inttofp_2_p2), .in14(fptoint_1_p2), .out(num_out), .sel(instruction));  // open: in15
  Multiplexer #(.select(4)) multiplexer_2 (
    .in0(comparator_1_gt), .in1(comparator_1_eq), .in2(comparator_1_lt), .in3(comparator_2_gt),
    .in4(comparator_2_eq), .in5(comparator_2_lt), .in6(fpcomparator_1_p3), .in7(fpcomparator_1_p4),
    .in8(fpcomparator_1_p5), .in9(1'b0), .in10(1'b0), .in11(1'b0), .in12(1'b0), .in13(1'b0), .in14(1'b0),
    .in15(1'b0), .out(comp_out), .sel(instruction));
endmodule

module instruction_decoder (
  input  [8:0] instruction,
  input  [2:0] sub_stage,
  input  carry,
  input  barrow,
  input  comp,
  output RSC,
  output MA_In,
  output M_I,
  output M_O,
  output IR_I,
  output IR_O,
  output PC_O,
  output PC_Up,
  output PC_jmp,
  output [3:0] ALU_inst,
  output A_I,
  output A_O,
  output N1_I,
  output N1_O,
  output N2_I,
  output N2_O,
  output R0I,
  output R0O,
  output R1I,
  output R1O,
  output R2I,
  output R2O,
  output HLT
);

  wire and_1_out, and_2_out, and_3_out, and_4_out, and_5_out, and_6_out, and_7_out, and_8_out, and_9_out,
       and_10_out, and_11_out, and_12_out, and_13_out, and_14_out, and_15_out, and_16_out, and_17_out,
       and_18_out, and_19_out, and_20_out, and_21_out, and_22_out, and_23_out, and_24_out, and_25_out,
       and_26_out, and_27_out, and_28_out, and_29_out, and_30_out, and_31_out, and_32_out, and_33_out,
       and_34_out, and_35_out, and_36_out, and_37_out, and_38_out, and_39_out, and_40_out, and_41_out,
       and_42_out, and_43_out, and_45_out, and_46_out, and_47_out, and_48_out, and_49_out, and_50_out,
       and_51_out, and_52_out, and_53_out, and_54_out, and_55_out, and_57_out, and_58_out, and_59_out,
       and_60_out, and_61_out, and_62_out, and_63_out, and_64_out, and_65_out, and_66_out, and_67_out,
       and_68_out, and_69_out, and_70_out, and_71_out, and_72_out, and_73_out, and_74_out, and_75_out,
       and_76_out, and_77_out, and_78_out, and_79_out, and_80_out, and_81_out, and_82_out, and_83_out,
       and_84_out, and_85_out, and_86_out, and_87_out, and_88_out, and_89_out, and_90_out, and_91_out,
       and_92_out, and_93_out, and_94_out, and_95_out, and_96_out, and_97_out, and_98_out, and_99_out,
       and_100_out, and_101_out, and_102_out, and_103_out, and_104_out, and_105_out, and_106_out,
       and_107_out, and_108_out, and_109_out, and_110_out, and_111_out, and_112_out, and_113_out,
       and_114_out, and_115_out, and_116_out, and_117_out, and_118_out, and_119_out, and_120_out,
       and_121_out, and_122_out, and_123_out, and_124_out, and_125_out, and_126_out, and_127_out,
       and_128_out, not_1_out, not_2_out, not_3_out, not_4_out, not_5_out, not_6_out, not_7_out, not_8_out,
       not_9_out, not_10_out, not_11_out, not_12_out, not_13_out, not_14_out;

  not not_1 (not_1_out, instruction[8]);
  not not_2 (not_2_out, instruction[7]);
  not not_3 (not_3_out, instruction[6]);
  not not_4 (not_4_out, instruction[5]);
  not not_5 (not_5_out, instruction[4]);
  not not_6 (not_6_out, instruction[3]);
  not not_7 (not_7_out, instruction[2]);
  not not_8 (not_8_out, instruction[1]);
  not not_9 (not_9_out, instruction[0]);
  not not_10 (not_10_out, sub_stage[2]);
  not not_11 (not_11_out, sub_stage[1]);
  not not_12 (not_12_out, sub_stage[0]);
  not not_13 (not_13_out, carry);
  not not_14 (not_14_out, comp);
  and and_1 (and_1_out, sub_stage[2], sub_stage[1], sub_stage[0]);
  and and_2 (and_2_out, not_1_out, not_2_out, not_3_out, not_4_out, not_5_out, not_6_out, instruction[2], instruction[1], instruction[0], not_10_out, sub_stage[1], not_12_out);
  and and_3 (and_3_out, not_1_out, not_2_out, not_3_out, not_4_out, not_5_out, instruction[3], not_7_out, not_8_out, instruction[0], sub_stage[2], sub_stage[0]);
  and and_4 (and_4_out, not_1_out, not_2_out, not_3_out, not_4_out, not_5_out, instruction[3], not_7_out, instruction[1], sub_stage[2], not_11_out, not_12_out);
  and and_5 (and_5_out, not_1_out, not_2_out, not_3_out, not_4_out, not_5_out, instruction[3], not_8_out, not_9_out, sub_stage[2], not_11_out, not_12_out);
  and and_6 (and_6_out, not_1_out, not_2_out, not_4_out, instruction[4], instruction[3], not_7_out, not_8_out, sub_stage[1], sub_stage[0]);
  and and_7 (and_7_out, not_1_out, not_2_out, not_4_out, instruction[4], instruction[3], not_7_out, not_9_out, sub_stage[1], sub_stage[0]);
  and and_8 (and_8_out, not_1_out, not_2_out, not_4_out, instruction[4], instruction[3], not_8_out, not_9_out, sub_stage[1], sub_stage[0]);
  and and_9 (and_9_out, not_1_out, not_2_out, not_3_out, instruction[5], not_5_out, sub_stage[1], sub_stage[0]);
  and and_10 (and_10_out, not_1_out, not_2_out, not_3_out, instruction[5], not_6_out, not_7_out, not_8_out, not_9_out, sub_stage[1], sub_stage[0]);
  and and_11 (and_11_out, not_1_out, not_2_out, not_3_out, instruction[5], instruction[4], not_6_out, not_7_out, instruction[1], not_9_out, not_10_out, sub_stage[1], not_13_out);
  and and_12 (and_12_out, not_1_out, not_2_out, not_3_out, instruction[4], not_6_out, not_7_out, instruction[1], sub_stage[2], not_11_out, not_12_out);
  and and_13 (and_13_out, not_1_out, not_2_out, not_3_out, instruction[5], instruction[4], not_6_out, not_7_out, instruction[1], instruction[0], not_10_out, sub_stage[1], carry);
  and and_14 (and_14_out, not_1_out, not_2_out, not_3_out, instruction[5], instruction[4], not_6_out, instruction[2], not_8_out, not_9_out, not_10_out, sub_stage[1], not_14_out);
  and and_15 (and_15_out, not_1_out, not_2_out, not_3_out, instruction[4], not_6_out, instruction[2], not_8_out, sub_stage[2], not_11_out, not_12_out);
  and and_16 (and_16_out, not_1_out, not_2_out, not_3_out, instruction[5], instruction[4], not_6_out, instruction[2], not_8_out, instruction[0], not_10_out, sub_stage[1], comp);
  and and_17 (and_17_out, not_1_out, not_2_out, instruction[6], not_5_out, not_7_out, instruction[1], sub_stage[1], sub_stage[0]);
  and and_18 (and_18_out, not_1_out, not_2_out, instruction[6], not_4_out, instruction[4], not_7_out, not_8_out, sub_stage[1], sub_stage[0]);
  and and_19 (and_19_out, not_1_out, not_2_out, instruction[6], not_4_out, not_6_out, not_7_out, instruction[0], sub_stage[1], sub_stage[0]);
  and and_20 (and_20_out, not_1_out, not_2_out, instruction[5], not_5_out, not_6_out, not_7_out, sub_stage[1], sub_stage[0]);
  and and_21 (and_21_out, not_1_out, not_2_out, instruction[6], instruction[5], not_5_out, instruction[3], not_7_out, not_8_out, not_9_out, sub_stage[2], not_11_out, not_12_out);
  and and_22 (and_22_out, not_1_out, not_2_out, instruction[5], not_5_out, not_7_out, instruction[0], sub_stage[1], sub_stage[0]);
  and and_23 (and_23_out, not_1_out, not_2_out, instruction[6], not_4_out, instruction[3], not_8_out, not_9_out, sub_stage[1], sub_stage[0]);
  and and_24 (and_24_out, not_1_out, not_2_out, instruction[6], not_5_out, instruction[3], instruction[2], not_8_out, not_9_out, sub_stage[1], sub_stage[0]);
  and and_25 (and_25_out, not_1_out, not_2_out, not_4_out, not_5_out, not_6_out, instruction[2], not_8_out, not_9_out, sub_stage[1], sub_stage[0]);
  and and_26 (and_26_out, not_1_out, not_2_out, not_3_out, not_5_out, not_6_out, not_8_out, instruction[0], sub_stage[1], sub_stage[0]);
  and and_27 (and_27_out, not_1_out, not_2_out, not_3_out, not_5_out, not_6_out, instruction[1], not_9_out, sub_stage[1], sub_stage[0]);
  and and_28 (and_28_out, not_1_out, not_2_out, not_5_out, not_6_out, not_7_out, instruction[0], sub_stage[1], sub_stage[0]);
  and and_29 (and_29_out, not_1_out, not_2_out, not_3_out, not_4_out, instruction[4], not_6_out, not_7_out, sub_stage[2], not_11_out, not_12_out);
  and and_30 (and_30_out, not_1_out, not_2_out, not_3_out, instruction[4], not_6_out, not_7_out, instruction[0], sub_stage[2], not_11_out, not_12_out);
  and and_31 (and_31_out, not_10_out, not_11_out, not_12_out);
  and and_32 (and_32_out, not_1_out, not_2_out, not_3_out, not_4_out, not_5_out, instruction[3], not_7_out, not_8_out, instruction[0], not_10_out, sub_stage[1], sub_stage[0]);
  and and_33 (and_33_out, not_1_out, not_2_out, not_3_out, not_4_out, not_5_out, instruction[3], not_7_out, instruction[1], not_10_out, not_12_out);
  and and_34 (and_34_out, not_1_out, not_2_out, not_3_out, not_4_out, not_5_out, instruction[3], not_8_out, not_9_out, not_10_out, not_12_out);
  and and_35 (and_35_out, not_1_out, not_2_out, not_3_out, not_4_out, instruction[4], not_6_out, not_7_out, instruction[1], not_9_out, sub_stage[1], not_12_out);
  and and_36 (and_36_out, not_1_out, not_2_out, not_3_out, not_4_out, instruction[4], not_6_out, not_7_out, not_10_out, not_12_out);
  and and_37 (and_37_out, not_1_out, not_2_out, not_3_out, not_4_out, instruction[4], not_6_out, not_8_out, not_10_out, not_12_out);
  and and_38 (and_38_out, not_1_out, not_2_out, not_3_out, not_4_out, instruction[4], not_6_out, not_7_out, not_10_out, sub_stage[1], sub_stage[0]);
  and and_39 (and_39_out, not_1_out, not_2_out, not_3_out, not_4_out, instruction[4], not_6_out, not_8_out, not_10_out, sub_stage[1], sub_stage[0]);
  and and_40 (and_40_out, not_10_out, not_11_out, sub_stage[0]);
  and and_41 (and_41_out, not_1_out, not_2_out, not_3_out, not_4_out, not_5_out, instruction[3], not_7_out, not_8_out, instruction[0], sub_stage[2], not_11_out, not_12_out);
  and and_42 (and_42_out, not_1_out, not_2_out, not_3_out, not_4_out, not_5_out, instruction[3], not_7_out, instruction[1], not_10_out, sub_stage[0]);
  and and_43 (and_43_out, not_1_out, not_2_out, not_3_out, not_4_out, not_5_out, instruction[3], not_8_out, not_9_out, not_10_out, sub_stage[0]);
  and and_44 (IR_I, not_10_out, not_11_out, sub_stage[0]);
  and and_45 (and_45_out, not_1_out, not_2_out, not_3_out, not_4_out, instruction[3], not_8_out, not_9_out, not_10_out, sub_stage[1], not_12_out);
  and and_46 (and_46_out, not_1_out, not_2_out, not_3_out, not_4_out, instruction[4], not_7_out, not_10_out, sub_stage[1], not_12_out);
  and and_47 (and_47_out, not_1_out, not_2_out, not_3_out, not_4_out, instruction[4], not_6_out, not_8_out, not_10_out, sub_stage[1], not_12_out);
  and and_48 (and_48_out, not_1_out, not_2_out, not_3_out, not_4_out, not_5_out, instruction[3], not_7_out, not_8_out, instruction[0], not_10_out, sub_stage[1], sub_stage[0]);
  and and_49 (and_49_out, not_1_out, not_2_out, not_3_out, not_4_out, instruction[4], not_6_out, not_7_out, instruction[1], not_9_out, sub_stage[1], not_12_out);
  and and_50 (and_50_out, not_1_out, not_2_out, not_3_out, not_4_out, instruction[3], not_7_out, instruction[1], not_10_out, sub_stage[1], not_12_out);
  and and_51 (and_51_out, not_1_out, not_2_out, not_3_out, instruction[5], instruction[4], not_6_out, instruction[2], not_8_out, not_9_out, not_10_out, sub_stage[1], comp);
  and and_52 (and_52_out, not_1_out, not_2_out, not_3_out, instruction[5], instruction[4], not_6_out, not_8_out, instruction[0], not_10_out, sub_stage[1], not_14_out);
  and and_53 (and_53_out, not_1_out, not_2_out, not_3_out, instruction[5], instruction[4], not_6_out, not_7_out, not_8_out, instruction[0], not_10_out, sub_stage[1]);
  and and_54 (and_54_out, not_1_out, not_2_out, not_3_out, instruction[5], instruction[4], not_6_out, not_7_out, instruction[1], not_9_out, not_10_out, sub_stage[1], carry);
  and and_55 (and_55_out, not_1_out, not_2_out, not_3_out, instruction[5], instruction[4], not_6_out, not_7_out, instruction[0], not_10_out, sub_stage[1], not_13_out);
  and and_56 (PC_O, not_10_out, not_11_out, not_12_out);
  and and_57 (and_57_out, not_10_out, not_11_out, sub_stage[0]);
  and and_58 (and_58_out, not_1_out, not_2_out, not_3_out, instruction[5], instruction[4], not_6_out, not_7_out, instruction[1], not_10_out, sub_stage[0]);
  and and_59 (and_59_out, not_1_out, not_2_out, not_3_out, instruction[5], instruction[4], not_6_out, instruction[2], not_8_out, not_10_out, sub_stage[0]);
  and and_60 (and_60_out, not_1_out, not_2_out, not_3_out, instruction[5], instruction[4], not_6_out, not_7_out, instruction[0], not_10_out, sub_stage[0]);
  and and_61 (and_61_out, not_1_out, not_2_out, not_3_out, instruction[5], instruction[4], not_6_out, not_7_out, instruction[0], not_10_out, sub_stage[1], not_13_out);
  and and_62 (and_62_out, not_1_out, not_2_out, not_3_out, instruction[5], instruction[4], not_6_out, not_8_out, instruction[0], not_10_out, sub_stage[1], not_14_out);
  and and_63 (and_63_out, not_1_out, not_2_out, not_3_out, instruction[5], instruction[4], not_6_out, instruction[2], not_8_out, not_9_out, not_10_out, sub_stage[1], comp);
  and and_64 (and_64_out, not_1_out, not_2_out, not_3_out, instruction[5], instruction[4], not_6_out, not_7_out, instruction[1], not_9_out, not_10_out, sub_stage[1], carry);
  and and_65 (and_65_out, not_1_out, not_2_out, not_3_out, instruction[5], instruction[4], not_6_out, not_7_out, not_8_out, instruction[0], not_10_out, sub_stage[1]);
  and and_66 (and_66_out, not_1_out, not_2_out, not_3_out, instruction[5], not_5_out, not_6_out, instruction[1], not_10_out, sub_stage[1], not_12_out);
  and and_67 (and_67_out, not_1_out, not_2_out, not_3_out, instruction[5], not_5_out, not_6_out, instruction[2], not_10_out, sub_stage[1], not_12_out);
  and and_68 (and_68_out, not_1_out, not_2_out, not_3_out, instruction[5], instruction[4], not_6_out, not_7_out, not_8_out, not_9_out, not_10_out, sub_stage[1], not_12_out);
  and and_69 (and_69_out, not_1_out, not_2_out, not_3_out, instruction[5], not_5_out, not_6_out, instruction[0], not_10_out, sub_stage[1], not_12_out);
  and and_70 (and_70_out, not_1_out, not_2_out, not_3_out, not_5_out, not_6_out, instruction[2], instruction[1], not_10_out, sub_stage[1], not_12_out);
  and and_71 (and_71_out, not_1_out, not_2_out, not_3_out, instruction[5], not_5_out, not_6_out, not_7_out, not_8_out, not_9_out, not_10_out, sub_stage[1], not_12_out);
  and and_72 (and_72_out, not_1_out, not_2_out, not_3_out, instruction[5], not_5_out, instruction[3], instruction[2], not_10_out, sub_stage[1], not_12_out);
  and and_73 (and_73_out, not_1_out, not_2_out, not_3_out, not_5_out, not_6_out, instruction[2], instruction[0], not_10_out, sub_stage[1], not_12_out);
  and and_74 (and_74_out, not_1_out, not_2_out, not_3_out, not_5_out, not_6_out, instruction[2], not_8_out, not_9_out, not_10_out, sub_stage[1], not_12_out);
  and and_75 (and_75_out, not_1_out, not_2_out, not_3_out, instruction[5], not_5_out, not_6_out, not_8_out, not_9_out, not_10_out, sub_stage[1], not_12_out);
  and and_76 (and_76_out, not_1_out, not_2_out, not_3_out, instruction[5], not_5_out, instruction[3], instruction[1], not_10_out, sub_stage[1], not_12_out);
  and and_77 (and_77_out, not_1_out, not_2_out, not_3_out, not_5_out, not_6_out, instruction[1], instruction[0], not_10_out, sub_stage[1], not_12_out);
  and and_78 (and_78_out, not_1_out, not_2_out, not_3_out, not_5_out, not_6_out, instruction[1], not_9_out, not_10_out, sub_stage[1], not_12_out);
  and and_79 (and_79_out, not_1_out, not_2_out, not_3_out, not_5_out, not_6_out, instruction[2], not_9_out, not_10_out, sub_stage[1], not_12_out);
  and and_80 (and_80_out, not_1_out, not_2_out, not_3_out, instruction[5], not_5_out, not_6_out, not_9_out, not_10_out, sub_stage[1], not_12_out);
  and and_81 (and_81_out, not_1_out, not_2_out, not_3_out, instruction[5], not_5_out, instruction[3], instruction[0], not_10_out, sub_stage[1], not_12_out);
  and and_82 (and_82_out, not_1_out, not_2_out, not_3_out, not_5_out, not_6_out, instruction[2], not_8_out, not_10_out, sub_stage[1], not_12_out);
  and and_83 (and_83_out, not_1_out, not_2_out, not_3_out, instruction[5], not_5_out, not_10_out, sub_stage[1], not_12_out);
  and and_84 (and_84_out, not_1_out, not_2_out, not_3_out, instruction[5], not_6_out, not_7_out, not_8_out, not_9_out, not_10_out, sub_stage[1], not_12_out);
  and and_85 (and_85_out, not_1_out, not_2_out, not_3_out, not_5_out, not_6_out, instruction[0], not_10_out, sub_stage[1], not_12_out);
  and and_86 (and_86_out, not_1_out, not_2_out, not_3_out, not_5_out, not_6_out, not_7_out, instruction[1], not_10_out, sub_stage[1], not_12_out);
  and and_87 (and_87_out, not_1_out, not_2_out, instruction[6], instruction[5], not_5_out, instruction[3], not_7_out, instruction[0], not_10_out, sub_stage[1], not_12_out);
  and and_88 (and_88_out, not_1_out, not_2_out, instruction[6], instruction[5], not_5_out, instruction[3], not_7_out, instruction[1], not_10_out, sub_stage[1], not_12_out);
  and and_89 (and_89_out, not_1_out, not_2_out, instruction[6], instruction[5], not_5_out, instruction[3], instruction[2], not_8_out, not_9_out, not_10_out, sub_stage[1], not_12_out);
  and and_90 (and_90_out, not_1_out, not_2_out, not_3_out, not_4_out, instruction[4], not_6_out, instruction[2], not_8_out, instruction[0], not_10_out, sub_stage[1], sub_stage[0]);
  and and_91 (and_91_out, not_1_out, not_2_out, instruction[6], instruction[5], not_5_out, instruction[3], not_7_out, not_8_out, not_9_out, not_10_out, sub_stage[1], sub_stage[0]);
  and and_92 (and_92_out, not_1_out, not_2_out, not_4_out, instruction[4], instruction[3], not_7_out, not_8_out, not_9_out, not_10_out, sub_stage[1], not_12_out);
  and and_93 (and_93_out, not_1_out, not_2_out, instruction[6], not_4_out, instruction[3], not_7_out, not_8_out, not_9_out, not_10_out, sub_stage[1], not_12_out);
  and and_94 (and_94_out, not_1_out, not_2_out, instruction[6], not_4_out, instruction[4], not_7_out, not_8_out, not_9_out, not_10_out, sub_stage[1], not_12_out);
  and and_95 (and_95_out, not_1_out, not_2_out, instruction[6], instruction[5], not_5_out, not_6_out, not_7_out, not_8_out, not_9_out, not_10_out, sub_stage[1], not_12_out);
  and and_96 (and_96_out, not_1_out, not_2_out, not_3_out, not_4_out, not_5_out, instruction[3], not_7_out, not_8_out, not_9_out, not_10_out, sub_stage[1], sub_stage[0]);
  and and_97 (and_97_out, not_1_out, not_2_out, instruction[6], instruction[5], not_5_out, instruction[3], not_7_out, not_8_out, not_9_out, not_10_out, sub_stage[1], sub_stage[0]);
  and and_98 (and_98_out, not_1_out, not_2_out, instruction[6], not_4_out, not_5_out, not_6_out, not_7_out, instruction[0], not_10_out, sub_stage[1], not_12_out);
  and and_99 (and_99_out, not_1_out, not_2_out, instruction[6], not_4_out, not_5_out, not_6_out, not_7_out, instruction[1], not_10_out, sub_stage[1], not_12_out);
  and and_100 (and_100_out, not_1_out, not_2_out, instruction[6], not_4_out, not_5_out, not_6_out, instruction[2], not_8_out, not_9_out, not_10_out, sub_stage[1], not_12_out);
  and and_101 (and_101_out, not_1_out, not_2_out, not_3_out, not_4_out, instruction[4], not_6_out, not_7_out, not_8_out, not_9_out, not_10_out, sub_stage[1], sub_stage[0]);
  and and_102 (and_102_out, not_1_out, not_2_out, not_4_out, instruction[4], instruction[3], not_7_out, not_8_out, instruction[0], not_10_out, sub_stage[1], not_12_out);
  and and_103 (and_103_out, not_1_out, not_2_out, instruction[6], instruction[5], not_5_out, not_7_out, not_8_out, instruction[0], not_10_out, sub_stage[1], not_12_out);
  and and_104 (and_104_out, not_1_out, not_2_out, not_3_out, not_4_out, not_5_out, instruction[3], not_7_out, not_8_out, instruction[0], sub_stage[2], not_11_out, not_12_out);
  and and_105 (and_105_out, not_1_out, not_2_out, instruction[6], not_4_out, not_6_out, not_7_out, not_8_out, instruction[0], not_10_out, sub_stage[1], not_12_out);
  and and_106 (and_106_out, not_1_out, not_2_out, instruction[6], not_4_out, not_5_out, instruction[3], not_7_out, instruction[1], not_10_out, sub_stage[1], not_12_out);
  and and_107 (and_107_out, not_1_out, not_2_out, instruction[6], not_4_out, not_5_out, instruction[3], not_8_out, not_9_out, not_10_out, sub_stage[1], not_12_out);
  and and_108 (and_108_out, not_1_out, not_2_out, not_3_out, not_4_out, instruction[4], not_6_out, not_7_out, not_8_out, instruction[0], not_10_out, sub_stage[1], sub_stage[0]);
  and and_109 (and_109_out, not_1_out, not_2_out, not_4_out, instruction[4], instruction[3], not_7_out, instruction[1], not_9_out, not_10_out, sub_stage[1], not_12_out);
  and and_110 (and_110_out, not_1_out, not_2_out, instruction[6], not_5_out, not_7_out, instruction[1], not_9_out, not_10_out, sub_stage[1], not_12_out);
  and and_111 (and_111_out, not_1_out, not_2_out, not_3_out, not_4_out, not_5_out, instruction[3], not_7_out, instruction[1], not_9_out, not_10_out, sub_stage[1], sub_stage[0]);
  and and_112 (and_112_out, not_1_out, not_2_out, instruction[6], not_4_out, instruction[4], not_6_out, not_7_out, instruction[0], not_10_out, sub_stage[1], not_12_out);
  and and_113 (and_113_out, not_1_out, not_2_out, instruction[6], not_4_out, instruction[4], not_6_out, not_8_out, not_9_out, not_10_out, sub_stage[1], not_12_out);
  and and_114 (and_114_out, not_1_out, not_2_out, not_3_out, not_4_out, instruction[4], not_6_out, not_7_out, instruction[1], not_9_out, not_10_out, sub_stage[1], sub_stage[0]);
  and and_115 (and_115_out, not_1_out, not_2_out, not_3_out, not_4_out, instruction[4], instruction[3], not_7_out, instruction[1], instruction[0], not_10_out, sub_stage[1], not_12_out);
  and and_116 (and_116_out, not_1_out, not_2_out, instruction[6], not_5_out, not_7_out, instruction[1], instruction[0], not_10_out, sub_stage[1], not_12_out);
  and and_117 (and_117_out, not_1_out, not_2_out, instruction[6], not_4_out, not_6_out, not_7_out, instruction[1], instruction[0], not_10_out, sub_stage[1], not_12_out);
  and and_118 (and_118_out, not_1_out, not_2_out, not_3_out, not_4_out, not_5_out, instruction[3], not_7_out, instruction[1], instruction[0], not_10_out, sub_stage[1], sub_stage[0]);
  and and_119 (and_119_out, not_1_out, not_2_out, instruction[6], not_4_out, instruction[4], instruction[3], not_7_out, not_8_out, not_10_out, sub_stage[1], not_12_out);
  and and_120 (and_120_out, not_1_out, not_2_out, instruction[6], not_4_out, instruction[4], instruction[3], not_7_out, not_9_out, not_10_out, sub_stage[1], not_12_out);
  and and_121 (and_121_out, not_1_out, not_2_out, instruction[6], not_4_out, instruction[4], instruction[3], not_8_out, not_9_out, not_10_out, sub_stage[1], not_12_out);
  and and_122 (and_122_out, not_1_out, not_2_out, not_3_out, not_4_out, instruction[4], not_6_out, not_7_out, instruction[1], instruction[0], not_10_out, sub_stage[1], sub_stage[0]);
  and and_123 (and_123_out, not_1_out, not_2_out, not_4_out, instruction[4], instruction[3], instruction[2], not_8_out, not_9_out, not_10_out, sub_stage[1], not_12_out);
  and and_124 (and_124_out, not_1_out, not_2_out, instruction[6], not_4_out, instruction[2], not_8_out, not_9_out, not_10_out, sub_stage[1], not_12_out);
  and and_125 (and_125_out, not_1_out, not_2_out, instruction[6], not_5_out, instruction[3], instruction[2], not_8_out, not_9_out, not_10_out, sub_stage[1], not_12_out);
  and and_126 (and_126_out, not_1_out, not_2_out, not_3_out, not_4_out, not_5_out, instruction[3], instruction[2], not_8_out, not_9_out, not_10_out, sub_stage[1], sub_stage[0]);
  and and_127 (and_127_out, not_1_out, not_2_out, instruction[6], instruction[5], not_5_out, not_6_out, not_7_out, not_10_out, sub_stage[1], not_12_out);
  and and_128 (and_128_out, not_1_out, not_2_out, not_3_out, not_4_out, instruction[4], not_6_out, instruction[2], not_8_out, not_9_out, not_10_out, sub_stage[1], sub_stage[0]);
  and and_129 (HLT, instruction[8], instruction[7], instruction[6], instruction[5], instruction[4], instruction[3], instruction[2], instruction[1], instruction[0], not_10_out, sub_stage[1], not_12_out);
  or or_1 (MA_In, and_31_out, and_32_out, and_33_out, and_34_out, and_35_out, and_36_out, and_37_out);
  or or_2 (M_I, and_38_out, and_39_out);
  or or_3 (M_O, and_40_out, and_41_out, and_42_out, and_43_out);
  or or_4 (PC_Up, and_57_out, and_58_out, and_59_out, and_60_out);
  or or_5 (PC_jmp, and_61_out, and_62_out, and_63_out, and_64_out, and_65_out);
  or or_6 (ALU_inst[3], and_66_out, and_67_out, and_68_out, and_69_out);
  or or_7 (ALU_inst[2], and_70_out, and_71_out, and_72_out, and_73_out);
  or or_8 (ALU_inst[1], and_74_out, and_75_out, and_76_out, and_77_out);
  or or_9 (ALU_inst[0], and_78_out, and_79_out, and_80_out, and_81_out);
  or or_10 (A_I, and_82_out, and_83_out, and_84_out, and_85_out, and_86_out);
  or or_11 (A_O, and_87_out, and_88_out, and_89_out, and_90_out, and_91_out);
  or or_12 (N1_I, and_92_out, and_93_out, and_94_out, and_95_out, and_96_out, and_97_out);
  or or_13 (N1_O, and_98_out, and_99_out, and_100_out, and_101_out);
  or or_14 (N2_I, and_102_out, and_103_out, and_104_out, and_105_out);
  or or_15 (N2_O, and_106_out, and_107_out, and_108_out);
  or or_16 (R0I, and_109_out, and_110_out, and_111_out);
  or or_17 (R0O, and_112_out, and_113_out, and_114_out);
  or or_18 (R1I, and_115_out, and_116_out, and_117_out, and_118_out);
  or or_19 (R1O, and_119_out, and_120_out, and_121_out, and_122_out);
  or or_20 (R2I, and_123_out, and_124_out, and_125_out, and_126_out);
  or or_21 (R2O, and_127_out, and_128_out);
  or or_22 (IR_O, and_45_out, and_46_out, and_47_out, and_48_out, and_49_out, and_50_out, and_51_out, and_52_out, and_53_out, and_54_out, and_55_out);
  or or_23 (RSC, and_1_out, and_2_out, and_3_out, and_4_out, and_5_out, and_6_out, and_7_out, and_8_out, and_9_out, and_10_out, and_11_out, and_12_out, and_13_out, and_14_out, and_15_out, and_16_out, and_17_out, and_18_out, and_19_out, and_20_out, and_21_out, and_22_out, and_23_out, and_24_out, and_25_out, and_26_out, and_27_out, and_28_out, and_29_out, and_30_out);
endmodule
