// Logisim project curcuit.circ as structural Verilog: 20 circuits, main circuit main
module main (
);

  wire and_1_out, clck, cpu_1_ml, cpu_1_mw, cpu_1_preveledge, d_ff_1_qn, dsp1_1W, dsp1_2W, dsp2_1W, dsp2_2W,
       dsp3_1W, dsp3_2W, HLT, interuptr_1_interupt, keyboard_1_avail, mcmu_1_rl, mcmu_1_rw, mcmu_1_stall,
       mcmu_1_vcmw, or_1_out, or_2_out, reset, Vclck, vgacard_1_pic, vmcu_1_busy;
  wire [1:0] interuptr_1_interuptdevid;
  wire [2:0] ODD;
  wire [6:0] keyboard_1_data, rgb_video_5_p4, rgb_video_6_p4;
  wire [7:0] dsp_x_cod, dsp_y_cod;
  wire [9:0] vgacard_1_h, vgacard_1_v;
  wire [18:0] bit_extender_1_out, vgacard_1_pxcod;
  wire [23:0] bit_extender_2_out, cpu_1_adr, mcmu_1_adress, multiplexer_1_out, pxD;
  wire [31:0] cpu_1_data, interuptr_1_data, multiplexer_2_out, OD1, OD2, ram_1_dout;

  Keyboard keyboard_1 (.clk(clck), .re(1'b1), .clr(1'b0), .avail(keyboard_1_avail), .data(keyboard_1_data));
  Interuptr interuptr_1 (
    .KBAvb(keyboard_1_avail), .KBChar(keyboard_1_data), .interupt(interuptr_1_interupt),
    .InteruptDevID(interuptr_1_interuptdevid), .data(interuptr_1_data));
  or or_1 (or_1_out, interuptr_1_interupt, mcmu_1_stall);
  MCMU mcmu_1 (
    .adr(cpu_1_adr), .VCMB(vmcu_1_busy), .W(cpu_1_mw), .Rd(cpu_1_ml), .privilege(cpu_1_preveledge),
    .Clock(clck), .R(reset), .Adress(mcmu_1_adress), .stall(mcmu_1_stall), .VCMW(mcmu_1_vcmw),
    .RW(mcmu_1_rw), .RL(mcmu_1_rl));
  vgaCard vgacard_1 (
    .R(reset), .En(1'b1), .clock(Vclck), .nig(1'b0), .H(vgacard_1_h), .V(vgacard_1_v), .pic(vgacard_1_pic),
    .pxCod(vgacard_1_pxcod));  // open: HS, VS
  or or_2 (or_2_out, interuptr_1_interupt, mcmu_1_rw);
  and and_1 (and_1_out, Vclck, vgacard_1_pic);
  CPU cpu_1 (
    .reset(reset), .MemData(ram_1_dout), .C(clck), .InteruptDevID(interuptr_1_interuptdevid),
    .interupt(interuptr_1_interupt), .HLT(HLT), .stall(or_1_out), .Preveledge(cpu_1_preveledge), .OD1(OD1),
    .adr(cpu_1_adr), .data(cpu_1_data), .ML(cpu_1_ml), .MW(cpu_1_mw), .ODD(ODD), .OD2(OD2));
  RAM #(.addrWidth(24), .dataWidth(32)) ram_1 (
    .addr(multiplexer_1_out), .we(or_2_out), .oe(mcmu_1_rl), .clk(clck), .din(multiplexer_2_out),
    .dout(ram_1_dout));
  Multiplexer #(.width(24)) multiplexer_1 (
    .in0(mcmu_1_adress), .in1(24'hfb4efa), .out(multiplexer_1_out), .sel(interuptr_1_interupt));
  Multiplexer #(.width(32)) multiplexer_2 (
    .in0(cpu_1_data), .in1(interuptr_1_data), .out(multiplexer_2_out), .sel(interuptr_1_interupt));
  Bit_Extender #(.in_width(24), .out_width(19), .\type ("zero")) bit_extender_1 (
    .in(mcmu_1_adress), .out(bit_extender_1_out));
  Bit_Extender #(.in_width(32), .out_width(24), .\type ("zero")) bit_extender_2 (
    .in(cpu_1_data), .out(bit_extender_2_out));
  Clock clock_1 (.out(clck));
  DipSwitch #(.number(2)) dipswitch_1 (.sw2(HLT));  // open: sw1
  VMCU vmcu_1 (
    .R(reset), .VCC(and_1_out), .VDA(vgacard_1_pxcod), .SDA(bit_extender_1_out), .W(mcmu_1_vcmw),
    .SD(bit_extender_2_out), .RC(clck), .busy(vmcu_1_busy), .VDO(pxD));
  D_Flip_Flop d_ff_1 (.D(d_ff_1_qn), .clk(clck), .Q(Vclck), .Qn(d_ff_1_qn), .preset(reset));  // open: reset
  Bit_Extender #(.in_width(10), .out_width(8)) bit_extender_3 (.in(vgacard_1_h), .out(dsp_x_cod));
  Bit_Extender #(.in_width(10), .out_width(8)) bit_extender_4 (.in(vgacard_1_v), .out(dsp_y_cod));
  Button R (.out(reset));
  // RGB_Video #(.height(256), .scale(1), .width(256)) rgb_video_1: pin names not known; wires that end beside it: reset, Vclck, dsp1_1W, dsp_x_cod, dsp_y_cod, pxD
  // RGB_Video #(.height(256), .scale(1), .width(256)) rgb_video_2: pin names not known; wires that end beside it: reset, Vclck, dsp1_2W, dsp_x_cod, dsp_y_cod, pxD
  dspCNT dspcnt_1 (
    .x_cod(vgacard_1_h), .y_cod(vgacard_1_v), .d1_1(dsp1_1W), .d1_2(dsp2_1W), .d1_3(dsp3_1W), .d2_1(dsp1_2W),
    .d2_2(dsp2_2W), .d2_3(dsp3_2W));
  // RGB_Video #(.height(256), .scale(1), .width(256)) rgb_video_3: pin names not known; wires that end beside it: reset, Vclck, dsp2_1W, dsp_x_cod, dsp_y_cod, pxD
  // RGB_Video #(.height(256), .scale(1), .width(256)) rgb_video_4: pin names not known; wires that end beside it: reset, Vclck, dsp2_2W, dsp_x_cod, dsp_y_cod, pxD
  // RGB_Video #(.height(256), .scale(1)) rgb_video_5: pin names not known; wires that end beside it: reset, Vclck, dsp3_1W, rgb_video_5_p4, dsp_y_cod, pxD
  // RGB_Video #(.height(256), .scale(1)) rgb_video_6: pin names not known; wires that end beside it: reset, Vclck, dsp3_2W, rgb_video_6_p4, dsp_y_cod, pxD
  Bit_Extender #(.out_width(7), .\type ("zero")) bit_extender_5 (.in(dsp_x_cod), .out(rgb_video_6_p4));
  Bit_Extender #(.out_width(7), .\type ("zero")) bit_extender_6 (.in(dsp_x_cod), .out(rgb_video_5_p4));
endmodule

module ProgramCounter (
  input  [31:0] JmpAddr,
  input  Reset,
  input  Jmp,
  input  Clock,
  output [31:0] ip
);

  wire [31:0] adder_1_out, multiplexer_1_out;

  Adder #(.width(32)) adder_1 (.a(ip), .b(32'h1), .out(adder_1_out));  // open: cin, cout
  Multiplexer #(.width(32)) multiplexer_1 (.in0(adder_1_out), .in1(JmpAddr), .out(multiplexer_1_out), .sel(Jmp));
  Register #(.width(32)) PC (.D(multiplexer_1_out), .en(1'b1), .Q(ip), .clk(Clock), .clr(Reset));
endmodule

module CPU (
  input  C,
  input  reset,
  input  [31:0] MemData,
  input  HLT,
  input  [1:0] InteruptDevID,
  input  stall,
  input  interupt,
  output [2:0] ODD,
  output [31:0] OD1,
  output [31:0] OD2,
  output [23:0] adr,
  output [31:0] data,
  output ML,
  output Preveledge,
  output MW
);

  wire ALU_Calc, and_1_out, and_2_out, and_3_out, and_4_out, and_5_out, button_1_out, DecSP, DRW,
       Executor_1_jmp, FDI, FRO, ICO, IncSP, IRAO, IRI, IRO, JMP, MABO, MO, nor_1_out, OD1W, OD2W, ODW, OEn,
       or_2_out, or_3_out, PCDBO, PCO, PCUp, Prev0, Prev1, priority_encoder_1_gs, R_out, reset_t, RetiIRI,
       RetiIRO, SCJAO, SPI, SPO, SR1O, SR2O;
  wire [1:0] priority_encoder_1_out;
  wire [2:0] ALU_1_p6, flags, ODD_t;
  wire [3:0] ALU_OP, DRID, SR1ID, SR2ID;
  wire [4:0] InstrDecoder_1_op;
  wire [23:0] adder_1_out, bit_extender_2_out, bit_extender_4_out, bit_extender_5_out, multiplexer_1_out,
       multiplexer_2_out, PC_q, register_4_q, SP_q, subtractor_1_out;
  wire [31:0] ALU_1_p8, bit_extender_1_out, bit_extender_6_out, IR_q, IRD, SR1, SR2;

  Button R (.out(R_out));
  assign bit_extender_1_out = {{8{1'b0}}, PC_q};  // Bit_Extender bit_extender_1
  or or_1 (reset_t, R_out, reset);
  assign data = PCDBO ? bit_extender_1_out : 32'bz;  // Controlled_Buffer controlled_buffer_1
  assign data = MO ? MemData : 32'bz;  // Controlled_Buffer controlled_buffer_2
  Bit_Extender #(.in_width(32), .out_width(24), .\type ("zero")) bit_extender_2 (
    .in(MemData), .out(bit_extender_2_out));
  assign adr = MABO ? bit_extender_2_out : 24'bz;  // Controlled_Buffer controlled_buffer_3
  Register #(.width(32)) IR (.D(data), .en(IRI), .clk(C), .Q(IR_q), .clr(reset_t));
  assign adr = PCO ? PC_q : 24'bz;  // Controlled_Buffer controlled_buffer_4
  Counter #(.max('hffffff), .ongoal("continue"), .width(24)) PC (
    .load(JMP), .D(adr), .count(PCUp), .Q(PC_q), .up(1'b1), .clk(C), .clr(reset_t));  // open: carry
  assign IRD = {{8{1'b0}}, IR_q[23:0]};  // Bit_Extender bit_extender_3
  assign adr = IRAO ? IR_q[23:0] : 24'bz;  // Controlled_Buffer controlled_buffer_5
  Priority_Encoder #(.select(2)) priority_encoder_1 (
    .in1(IncSP), .in2(DecSP), .in3(SPI), .out(priority_encoder_1_out), .gs(priority_encoder_1_gs),
    .en_in(1'b1));  // open: in0, en_out
  Multiplexer #(.select(2), .width(24)) multiplexer_1 (
    .in1(adder_1_out), .in2(subtractor_1_out), .in3(bit_extender_4_out), .out(multiplexer_1_out),
    .sel(priority_encoder_1_out));  // open: in0
  Bit_Extender #(.in_width(32), .out_width(24), .\type ("zero")) bit_extender_4 (.in(data), .out(bit_extender_4_out));
  assign data = IRO ? IRD : 32'bz;  // Controlled_Buffer controlled_buffer_6
  // ALU ALU_1: pin names not known; wires that end beside it: 1'b0, ALU_OP, SR1, SR2, IRD, ALU_1_p6[0], ALU_1_p6[1], ALU_1_p8, ALU_1_p6[2]
  Register #(.trigger("falling"), .width(24)) SP (
    .D(multiplexer_1_out), .en(priority_encoder_1_gs), .clk(C), .Q(SP_q), .clr(reset_t));
  assign adr = ICO ? multiplexer_2_out : 24'bz;  // Controlled_Buffer controlled_buffer_7
  Multiplexer #(.select(2), .width(24)) multiplexer_2 (
    .in1(24'hfb4efa), .out(multiplexer_2_out), .sel(InteruptDevID));  // open: in0, in2, in3
  Button button_1 (.out(button_1_out));
  assign data = ALU_Calc ? ALU_1_p8 : 32'bz;  // Controlled_Buffer controlled_buffer_8
  RegisterBank RegisterBank_1 (
    .C(C), .R(reset_t), .W(DRW), .RS1(SR1ID), .RS2(SR2ID), .DR(DRID), .DRD(data), .S1(SR1), .S2(SR2));
  Adder #(.width(24)) adder_1 (.a(SP_q), .b(24'h1), .out(adder_1_out));  // open: cin, cout
  Subtractor #(.width(24)) subtractor_1 (.a(SP_q), .b(24'h1), .out(subtractor_1_out));  // open: bin, bout
  assign adr = SPO ? SP_q : 24'bz;  // Controlled_Buffer controlled_buffer_9
  or or_2 (or_2_out, interupt, button_1_out);
  Register #(.width(3)) u_Flags (.D(ALU_1_p6), .en(ALU_Calc), .clk(C), .Q(flags), .clr(reset_t));
  assign data = SR1O ? SR1 : 32'bz;  // Controlled_Buffer controlled_buffer_10
  Bit_Extender #(.in_width(32), .out_width(24)) bit_extender_5 (.in(SR2), .out(bit_extender_5_out));
  InstrDecoder InstrDecoder_1 (
    .IR(IR_q), .flags(flags), .ALUOP(ALU_OP), .DR(DRID), .SR2(SR2ID), .SR1(SR1ID), .DDI(ODW), .OD1I(OD1W),
    .OD2I(OD2W), .ODD(ODD_t), .OP(InstrDecoder_1_op));
  nor nor_1 (nor_1_out, HLT, HLT);
  assign adr = SR2O ? bit_extender_5_out : 24'bz;  // Controlled_Buffer controlled_buffer_11
  and and_1 (and_1_out, nor_1_out, ~stall);  // AND_Gate
  Register #(.width(3)) register_1 (.D(ODD_t), .en(and_2_out), .clk(C), .Q(ODD), .clr(reset_t));
  and and_2 (and_2_out, ODW, OEn);
  Register #(.width(32)) register_2 (.D(data), .en(and_3_out), .clk(C), .Q(OD2), .clr(reset_t));
  and and_3 (and_3_out, OD2W, OEn);
  assign bit_extender_6_out = {{29{1'b0}}, flags};  // Bit_Extender bit_extender_6
  assign data = FRO ? bit_extender_6_out : 32'bz;  // Controlled_Buffer controlled_buffer_12
  assign adr = SCJAO ? 24'h40 : 24'bz;  // Controlled_Buffer controlled_buffer_13
  and and_4 (and_4_out, Preveledge, ~Prev0);  // AND_Gate
  D_Flip_Flop d_ff_1 (.D(or_3_out), .clk(C), .Q(Preveledge), .preset(reset_t));  // open: Qn, reset
  or or_3 (or_3_out, and_4_out, Prev1);
  Register #(.width(32)) register_3 (.D(data), .en(and_5_out), .clk(C), .Q(OD1), .clr(reset_t));
  and and_5 (and_5_out, OD1W, OEn);
  Register #(.width(24)) register_4 (.D(adr), .en(RetiIRI), .clk(C), .Q(register_4_q), .clr(reset_t));
  assign adr = RetiIRO ? register_4_q : 24'bz;  // Controlled_Buffer controlled_buffer_14
  Executor Executor_1 (
    .OP(InstrDecoder_1_op), .clock(C), .reset(reset_t), .Istop(and_1_out), .interupt(or_2_out),
    .JMP(Executor_1_jmp), .PCU(PCUp), .PCO(PCO), .PCDBO(PCDBO), .DRW(DRW), .SR1O(SR1O), .SR2O(SR2O),
    .ALUCalc(ALU_Calc), .MI(MW), .ML(ML), .MO(MO), .IRI(IRI), .IRO(IRO), .IRAO(IRAO), .MABO(MABO), .FDI(FDI),
    .OEn(OEn), .FRO(FRO), .SPInc(IncSP), .SPDec(DecSP), .SPI(SPI), .SPO(SPO), .ICAO(ICO), .Prv0(Prev0),
    .Prv1(Prev1), .SCJAO(SCJAO), .RetIRI(RetiIRI), .RetiIRO(RetiIRO));  // open: HLT

  // Other names for the same wires on the sheet: adr_bus[23:0] = adr; clck = C; data_bus[31:0] = data; MI = MW
endmodule

module ALU (
  input  Carry,
  input  [3:0] Op,
  input  [31:0] N1,
  input  [31:0] N2,
  output CO,
  output zero,
  output [31:0] A_O,
  output Comp
);

  wire comparator_1_eq, comparator_1_gt, comparator_1_lt, or_2_out, or_3_out;
  wire [4:0] bit_extender_1_out, bit_extender_2_out, bit_extender_3_out, bit_extender_4_out,
       bit_extender_5_out;
  wire [31:0] adder_1_out, and_1_out, multiplier_1_out, nand_1_out, negator_1_out, not_1_out, or_1_out,
       shifter_1_out, shifter_2_out, shifter_3_out, shifter_4_out, shifter_5_out, subtractor_1_out,
       xnor_1_out, xor_1_out;

  Bit_Extender #(.in_width(32), .out_width(5), .\type ("zero")) bit_extender_1 (.in(N2), .out(bit_extender_1_out));
  Bit_Extender #(.in_width(32), .out_width(5), .\type ("zero")) bit_extender_2 (.in(N2), .out(bit_extender_2_out));
  Bit_Extender #(.in_width(32), .out_width(5), .\type ("zero")) bit_extender_3 (.in(N2), .out(bit_extender_3_out));
  Bit_Extender #(.in_width(32), .out_width(5), .\type ("zero")) bit_extender_4 (.in(N2), .out(bit_extender_4_out));
  Bit_Extender #(.in_width(32), .out_width(5), .\type ("zero")) bit_extender_5 (.in(N2), .out(bit_extender_5_out));
  Adder #(.width(32)) adder_1 (.a(N1), .b(N2), .out(adder_1_out), .cin(Carry), .cout(CO));
  Subtractor #(.width(32)) subtractor_1 (.a(N1), .b(N2), .out(subtractor_1_out), .bin(1'b0));  // open: bout
  Multiplier #(.width(32)) multiplier_1 (.a(N1), .b(N2), .out(multiplier_1_out), .cin({32{1'b0}}));  // open: cout
  Negator #(.width(32)) negator_1 (.in(N1), .out(negator_1_out));
  assign and_1_out = N1 & N2;  // AND_Gate and_1, 32 bits wide
  assign or_1_out = N1 | N2;  // OR_Gate or_1, 32 bits wide
  assign not_1_out = ~N1;  // NOT_Gate not_1, 32 bits wide
  assign nand_1_out = ~(N1 & N2);  // NAND_Gate nand_1, 32 bits wide
  assign xor_1_out = N1 ^ N2;  // XOR_Gate xor_1, 32 bits wide
  assign xnor_1_out = ~(N1 ^ N2);  // XNOR_Gate xnor_1, 32 bits wide
  Shifter #(.width(32)) shifter_1 (.in(N1), .\dist (bit_extender_1_out), .out(shifter_1_out));
  Shifter #(.shift("lr"), .width(32)) shifter_2 (.in(N1), .\dist (bit_extender_2_out), .out(shifter_2_out));
  Shifter #(.shift("ar"), .width(32)) shifter_3 (.in(N1), .\dist (bit_extender_3_out), .out(shifter_3_out));
  Shifter #(.shift("rl"), .width(32)) shifter_4 (.in(N1), .\dist (bit_extender_4_out), .out(shifter_4_out));
  Shifter #(.shift("rr"), .width(32)) shifter_5 (.in(N1), .\dist (bit_extender_5_out), .out(shifter_5_out));
  Comparator #(.mode("unsigned"), .width(32)) comparator_1 (
    .a(N1), .b(N2), .gt(comparator_1_gt), .eq(comparator_1_eq), .lt(comparator_1_lt));
  or or_2 (or_2_out, comparator_1_gt, comparator_1_eq);
  or or_3 (or_3_out, comparator_1_eq, comparator_1_lt);
  Multiplexer #(.select(4), .width(32)) multiplexer_1 (
    .in0(adder_1_out), .in1(subtractor_1_out), .in2(multiplier_1_out), .in3(negator_1_out), .in4(and_1_out),
    .in5(or_1_out), .in6(not_1_out), .in7(nand_1_out), .in8(xor_1_out), .in9(xnor_1_out),
    .in10(shifter_1_out), .in11(shifter_2_out), .in12(shifter_3_out), .in13(shifter_4_out),
    .in14(shifter_5_out), .in15({32{1'b0}}), .out(A_O), .sel(Op));
  Multiplexer #(.select(4)) multiplexer_2 (
    .in0(comparator_1_gt), .in1(comparator_1_eq), .in2(comparator_1_lt), .in3(or_2_out), .in4(or_3_out),
    .in5(1'b0), .in6(1'b0), .in7(1'b0), .in8(1'b0), .in9(1'b0), .in10(1'b0), .in11(1'b0), .in12(1'b0),
    .in13(1'b0), .in14(1'b0), .in15(1'b0), .out(Comp), .sel(Op));
  and and_2 (zero, ~1'b1, ~A_O[0], ~A_O[1], ~A_O[2], ~A_O[3], ~A_O[4], ~A_O[5], ~A_O[6], ~A_O[7], ~A_O[8], ~A_O[9], ~A_O[10], ~A_O[11], ~A_O[12], ~A_O[13], ~A_O[14], ~A_O[15], ~A_O[16], ~A_O[17], ~A_O[18], ~A_O[19], ~A_O[20], ~A_O[21], ~A_O[22], ~A_O[23], ~A_O[24], ~A_O[25], ~A_O[26], ~A_O[27], ~A_O[28], ~A_O[29], ~A_O[30], ~A_O[31]);  // AND_Gate
endmodule

module RegisterBank (
  input  C,
  input  R,
  input  W,
  input  [3:0] RS1,
  input  [3:0] RS2,
  input  [3:0] DR,
  input  [31:0] DRD,
  output [31:0] S1,
  output [31:0] S2
);

  wire and_1_out, and_2_out, and_3_out, and_4_out, and_5_out, and_6_out, and_7_out, and_8_out, and_9_out,
       and_10_out, and_11_out, and_12_out, and_13_out, and_14_out, and_15_out, and_16_out, decoder_1_out0,
       decoder_1_out1, decoder_1_out2, decoder_1_out3, decoder_1_out4, decoder_1_out5, decoder_1_out6,
       decoder_1_out7, decoder_1_out8, decoder_1_out9, decoder_1_out10, decoder_1_out11, decoder_1_out12,
       decoder_1_out13, decoder_1_out14, decoder_1_out15;
  wire [31:0] R0_q, R1_q, R2_q, R3_q, R4_q, R5_q, R6_q, R7_q, R8_q, R9_q, R10_q, R11_q, R12_q, R13_q, R14_q,
       Tmp_q;

  Decoder #(.enable("false"), .select(4)) decoder_1 (
    .out0(decoder_1_out0), .out1(decoder_1_out1), .out2(decoder_1_out2), .out3(decoder_1_out3),
    .out4(decoder_1_out4), .out5(decoder_1_out5), .out6(decoder_1_out6), .out7(decoder_1_out7),
    .out8(decoder_1_out8), .out9(decoder_1_out9), .out10(decoder_1_out10), .out11(decoder_1_out11),
    .out12(decoder_1_out12), .out13(decoder_1_out13), .out14(decoder_1_out14), .out15(decoder_1_out15),
    .sel(DR));
  and and_1 (and_1_out, decoder_1_out0, W);
  Register #(.width(32)) R1 (.D(DRD), .en(and_2_out), .clk(C), .Q(R1_q), .clr(R));
  and and_2 (and_2_out, decoder_1_out1, W);
  and and_3 (and_3_out, decoder_1_out2, W);
  and and_4 (and_4_out, decoder_1_out3, W);
  and and_5 (and_5_out, decoder_1_out4, W);
  and and_6 (and_6_out, decoder_1_out5, W);
  Register #(.width(32)) R3 (.D(DRD), .en(and_4_out), .clk(C), .Q(R3_q), .clr(R));
  Register #(.width(32)) R5 (.D(DRD), .en(and_6_out), .clk(C), .Q(R5_q), .clr(R));
  and and_7 (and_7_out, decoder_1_out6, W);
  Register #(.width(32)) R7 (.D(DRD), .en(and_8_out), .clk(C), .Q(R7_q), .clr(R));
  and and_8 (and_8_out, decoder_1_out7, W);
  and and_9 (and_9_out, decoder_1_out8, W);
  Register #(.width(32)) R9 (.D(DRD), .en(and_10_out), .clk(C), .Q(R9_q), .clr(R));
  and and_10 (and_10_out, decoder_1_out9, W);
  and and_11 (and_11_out, decoder_1_out10, W);
  and and_12 (and_12_out, decoder_1_out11, W);
  and and_13 (and_13_out, decoder_1_out12, W);
  and and_14 (and_14_out, decoder_1_out13, W);
  Register #(.width(32)) R0 (.D(DRD), .en(and_1_out), .clk(C), .Q(R0_q), .clr(R));
  Register #(.width(32)) R2 (.D(DRD), .en(and_3_out), .clk(C), .Q(R2_q), .clr(R));
  Register #(.width(32)) R11 (.D(DRD), .en(and_12_out), .clk(C), .Q(R11_q), .clr(R));
  Register #(.width(32)) R13 (.D(DRD), .en(and_14_out), .clk(C), .Q(R13_q), .clr(R));
  and and_15 (and_15_out, decoder_1_out14, W);
  Register #(.width(32)) Tmp (.D(DRD), .en(and_16_out), .clk(C), .Q(Tmp_q), .clr(R));
  and and_16 (and_16_out, decoder_1_out15, W);
  Register #(.width(32)) R4 (.D(DRD), .en(and_5_out), .clk(C), .Q(R4_q), .clr(R));
  Register #(.width(32)) R6 (.D(DRD), .en(and_7_out), .clk(C), .Q(R6_q), .clr(R));
  Register #(.width(32)) R8 (.D(DRD), .en(and_9_out), .clk(C), .Q(R8_q), .clr(R));
  Register #(.width(32)) R10 (.D(DRD), .en(and_11_out), .clk(C), .Q(R10_q), .clr(R));
  Register #(.width(32)) R12 (.D(DRD), .en(and_13_out), .clk(C), .Q(R12_q), .clr(R));
  Register #(.width(32)) R14 (.D(DRD), .en(and_15_out), .clk(C), .Q(R14_q), .clr(R));
  Multiplexer #(.select(4), .width(32)) multiplexer_1 (
    .in0(R0_q), .in1(R1_q), .in2(R2_q), .in3(R3_q), .in4(R4_q), .in5(R5_q), .in6(R6_q), .in7(R7_q),
    .in8(R8_q), .in9(R9_q), .in10(R10_q), .in11(R11_q), .in12(R12_q), .in13(R13_q), .in14(R14_q),
    .in15(Tmp_q), .out(S1), .sel(RS1));
  Multiplexer #(.select(4), .width(32)) multiplexer_2 (
    .in0(R0_q), .in1(R1_q), .in2(R2_q), .in3(R3_q), .in4(R4_q), .in5(R5_q), .in6(R6_q), .in7(R7_q),
    .in8(R8_q), .in9(R9_q), .in10(R10_q), .in11(R11_q), .in12(R12_q), .in13(R13_q), .in14(R14_q),
    .in15(Tmp_q), .out(S2), .sel(RS2));

  // Notes on the sheet:
  //   R0
  //   R1
  //   R2
  //   R3
  //   R4
  //   R5
  //   R6
  //   R7
  //   R8\
  //   R9
  //   R10
  //   R11
  //   R12
  //   R13
  //   R14
  //   Tmp/Dump
endmodule

module InstrDecoder (
  input  [31:0] IR,
  input  [2:0] flags,
  output [3:0] ALUOP,
  output [3:0] DR,
  output [3:0] SR2,
  output [3:0] SR1,
  output DDI,
  output OD1I,
  output OD2I,
  output [2:0] ODD,
  output [4:0] OP
);

  wire and_2_out, and_3_out, InstrDecoderCA_1_sr1tdr, not_1_out, not_2_out;
  wire [3:0] InstrDecoderCA_1_pop;

  not not_1 (not_1_out, IR[7]);
  not not_2 (not_2_out, IR[8]);
  and and_1 (DDI, IR[7], not_2_out);
  and and_2 (and_2_out, not_1_out, not_2_out);
  and and_3 (and_3_out, IR[7], IR[8]);
  or or_1 (OD1I, and_2_out, and_3_out);
  InstrDecoderCA InstrDecoderCA_1 (
    .OP(IR[31:28]), .JMPIF(IR[26:24]), .carry(flags[0]), .Zero(flags[1]), .comp(flags[2]),
    .POP(InstrDecoderCA_1_pop), .SR1TDR(InstrDecoderCA_1_sr1tdr));
  Multiplexer #(.width(4)) multiplexer_1 (.in0(IR[19:16]), .in1(IR[27:24]), .out(DR), .sel(InstrDecoderCA_1_sr1tdr));
  InstrDcdL2 instrdcdl2_1 (.opI(InstrDecoderCA_1_pop), .JF(IR[27]), .SOT(IR[23:22]), .OP(OP));

  assign ALUOP = IR[15:12];
  assign OD2I = IR[8];
  assign ODD = IR[11:9];
  assign SR1 = IR[27:24];
  assign SR2 = IR[23:20];

  // Other names for the same wires on the sheet: carry = flags[0]; Zero = flags[1]; comp = flags[2]
endmodule

module InstrDecoderCA (
  input  [3:0] OP,
  input  [2:0] JMPIF,
  input  carry,
  input  Zero,
  input  comp,
  output [3:0] POP,
  output SR1TDR
);

  wire and_1_out, and_2_out, and_3_out, and_4_out, and_5_out, and_6_out, and_7_out, and_8_out, and_9_out,
       and_10_out, and_11_out, and_12_out, and_13_out, and_14_out, and_15_out, and_16_out, and_17_out,
       and_18_out, not_1_out, not_2_out, not_3_out, not_4_out, not_5_out, not_6_out, not_7_out, not_8_out,
       not_9_out;

  not not_1 (not_1_out, OP[3]);
  not not_2 (not_2_out, OP[1]);
  not not_3 (not_3_out, OP[0]);
  not not_4 (not_4_out, JMPIF[2]);
  not not_5 (not_5_out, JMPIF[1]);
  not not_6 (not_6_out, JMPIF[0]);
  not not_7 (not_7_out, carry);
  not not_8 (not_8_out, Zero);
  not not_9 (not_9_out, comp);
  and and_1 (and_1_out, OP[1], not_3_out);
  and and_2 (and_2_out, OP[1], not_4_out, not_5_out, carry);
  and and_3 (and_3_out, OP[1], not_4_out, not_6_out, not_7_out);
  and and_4 (and_4_out, OP[1], JMPIF[2], not_5_out, JMPIF[0], Zero);
  and and_5 (and_5_out, OP[1], JMPIF[2], JMPIF[1], not_6_out, not_8_out);
  and and_6 (and_6_out, OP[2], OP[1]);
  and and_7 (and_7_out, OP[3], OP[1]);
  and and_8 (and_8_out, OP[1], not_4_out, JMPIF[1], JMPIF[0], comp);
  and and_9 (and_9_out, OP[1], not_5_out, not_6_out, not_9_out);
  and and_10 (and_10_out, not_2_out, OP[0]);
  and and_11 (and_11_out, OP[0], not_4_out, not_5_out, carry);
  and and_12 (and_12_out, OP[0], not_4_out, not_6_out, not_7_out);
  and and_13 (and_13_out, OP[0], JMPIF[2], not_5_out, JMPIF[0], Zero);
  and and_14 (and_14_out, OP[0], JMPIF[2], JMPIF[1], not_6_out, not_8_out);
  and and_15 (and_15_out, OP[2], OP[0]);
  and and_16 (and_16_out, OP[3], OP[0]);
  and and_17 (and_17_out, OP[0], not_4_out, JMPIF[1], JMPIF[0], comp);
  and and_18 (and_18_out, OP[0], not_5_out, not_6_out, not_9_out);
  and and_19 (SR1TDR, not_1_out, OP[2], not_3_out);
  or or_1 (POP[1], and_1_out, and_2_out, and_3_out, and_4_out, and_5_out, and_6_out, and_7_out, and_8_out, and_9_out);
  or or_2 (POP[0], and_10_out, and_11_out, and_12_out, and_13_out, and_14_out, and_15_out, and_16_out, and_17_out, and_18_out);

  assign POP[3:2] = OP[3:2];
endmodule

module Executor (
  input  [4:0] OP,
  input  clock,
  input  reset,
  input  Istop,
  input  interupt,
  output JMP,
  output PCU,
  output PCO,
  output PCDBO,
  output DRW,
  output SR1O,
  output SR2O,
  output ALUCalc,
  output MI,
  output ML,
  output MO,
  output IRI,
  output IRO,
  output IRAO,
  output MABO,
  output FDI,
  output OEn,
  output FRO,
  output SPInc,
  output SPDec,
  output SPI,
  output SPO,
  output ICAO,
  output Prv0,
  output Prv1,
  output SCJAO,
  output RetIRI,
  output RetiIRO,
  output HLT
);

  wire and_1_out, andclock_11_o, button_1_out, d_ff_1_q, d_ff_2_qn, d_ff_3_q, ExecutorCA_1_drw,
       ExecutorCA_1_hlt, ExecutorCA_1_iri, ExecutorCA_1_jmp, ExecutorCA_1_jsc1, ExecutorCA_1_mi,
       ExecutorCA_1_ml, ExecutorCA_1_oen, ExecutorCA_1_pcu, ExecutorCA_1_retiri, ExecutorCA_1_retiro,
       ExecutorCA_1_rir, ExecutorCA_1_rsc, not_1_out, or_1_out, or_2_out, or_3_out, or_4_out, or_5_out;
  wire [2:0] counter_1_q;

  Button button_1 (.out(button_1_out));
  or or_1 (or_1_out, reset, and_1_out);
  or or_2 (or_2_out, interupt, button_1_out);
  Counter #(.max('h7), .width(3)) counter_1 (
    .clr(or_1_out), .load(andclock_11_o), .up(1'b1), .count(Istop), .clk(clock), .D(3'b001), .Q(counter_1_q));  // open: carry
  D_Flip_Flop d_ff_1 (.D(or_2_out), .clk(or_2_out), .Q(d_ff_1_q), .reset(or_3_out));  // open: Qn, preset
  or or_3 (or_3_out, reset, d_ff_3_q);
  D_Flip_Flop d_ff_2 (.D(ExecutorCA_1_rsc), .clk(clock), .Qn(d_ff_2_qn), .reset(reset));  // open: Q, preset
  and and_1 (and_1_out, ExecutorCA_1_rsc, d_ff_2_qn);
  D_Flip_Flop d_ff_3 (.D(d_ff_1_q), .clk(or_4_out), .Q(d_ff_3_q), .reset(or_5_out));  // open: Qn, preset
  or or_4 (or_4_out, ExecutorCA_1_jsc1, and_1_out);
  or or_5 (or_5_out, reset, ExecutorCA_1_rir);
  not not_1 (not_1_out, clock);
  ExecutorCA ExecutorCA_1 (
    .interrupt(d_ff_3_q), .OP(OP), .SBC(counter_1_q), .JMP(ExecutorCA_1_jmp), .PCU(ExecutorCA_1_pcu),
    .PCO(PCO), .PCDBO(PCDBO), .DRW(ExecutorCA_1_drw), .SR1O(SR1O), .SR2O(SR2O), .ALUCalc(ALUCalc),
    .MI(ExecutorCA_1_mi), .ML(ExecutorCA_1_ml), .MO(MO), .IRI(ExecutorCA_1_iri), .IRO(IRO), .IRAO(IRAO),
    .MOA(MABO), .FDI(FDI), .OEn(ExecutorCA_1_oen), .FRO(FRO), .SPInc(SPInc), .SPDec(SPDec), .SPI(SPI),
    .SPO(SPO), .ICAO(ICAO), .Prev0(Prv0), .Prev1(Prv1), .SCJAO(SCJAO), .RetIRI(ExecutorCA_1_retiri),
    .RetIRO(ExecutorCA_1_retiro), .HLT(ExecutorCA_1_hlt), .JSC1(ExecutorCA_1_jsc1), .RSC(ExecutorCA_1_rsc),
    .RIR(ExecutorCA_1_rir));
  andClock andclock_1 (.C(not_1_out), .S(ExecutorCA_1_jmp), .O(JMP));
  andClock andclock_2 (.C(not_1_out), .S(ExecutorCA_1_pcu), .O(PCU));
  andClock andclock_3 (.C(not_1_out), .S(ExecutorCA_1_drw), .O(DRW));
  andClock andclock_4 (.C(not_1_out), .S(ExecutorCA_1_mi), .O(MI));
  andClock andclock_5 (.C(not_1_out), .S(ExecutorCA_1_ml), .O(ML));
  andClock andclock_6 (.C(not_1_out), .S(ExecutorCA_1_iri), .O(IRI));
  andClock andclock_7 (.C(not_1_out), .S(ExecutorCA_1_oen), .O(OEn));
  andClock andclock_8 (.C(not_1_out), .S(ExecutorCA_1_retiri), .O(RetIRI));
  andClock andclock_9 (.C(not_1_out), .S(ExecutorCA_1_retiro), .O(RetiIRO));
  andClock andclock_10 (.C(not_1_out), .S(ExecutorCA_1_hlt), .O(HLT));
  andClock andclock_11 (.C(not_1_out), .S(ExecutorCA_1_jsc1), .O(andclock_11_o));
endmodule

module ExecutorCA (
  input  interrupt,
  input  [4:0] OP,
  input  [2:0] SBC,
  output JMP,
  output PCU,
  output PCO,
  output PCDBO,
  output DRW,
  output SR1O,
  output SR2O,
  output ALUCalc,
  output MI,
  output ML,
  output MO,
  output IRI,
  output IRO,
  output IRAO,
  output MOA,
  output FDI,
  output OEn,
  output FRO,
  output SPInc,
  output SPDec,
  output SPI,
  output SPO,
  output ICAO,
  output Prev0,
  output Prev1,
  output SCJAO,
  output RetIRI,
  output RetIRO,
  output HLT,
  output JSC1,
  output RSC,
  output RIR
);

  wire and_1_out, and_2_out, and_3_out, and_4_out, and_5_out, and_6_out, and_7_out, and_8_out, and_9_out,
       and_10_out, and_11_out, and_12_out, and_13_out, and_14_out, and_15_out, and_16_out, and_17_out,
       and_18_out, and_19_out, and_20_out, and_21_out, and_22_out, and_23_out, and_24_out, and_25_out,
       and_26_out, and_27_out, and_28_out, and_29_out, and_30_out, and_31_out, and_32_out, and_33_out,
       and_34_out, and_35_out, and_36_out, and_37_out, and_38_out, and_39_out, and_40_out, and_41_out,
       and_42_out, and_43_out, and_44_out, and_45_out, and_46_out, and_47_out, and_48_out, and_49_out,
       and_50_out, and_51_out, and_52_out, and_55_out, and_56_out, and_57_out, and_61_out, and_62_out,
       and_63_out, and_64_out, and_65_out, and_66_out, and_67_out, and_68_out, and_69_out, and_70_out,
       and_71_out, and_72_out, and_73_out, and_74_out, and_81_out, and_82_out, and_83_out, and_84_out,
       and_85_out, and_86_out, and_87_out, and_88_out, and_89_out, and_90_out, and_91_out, and_92_out,
       and_93_out, and_94_out, and_95_out, and_96_out, and_97_out, and_98_out, and_99_out, and_100_out,
       not_1_out, not_2_out, not_3_out, not_4_out, not_5_out, not_6_out, not_7_out, not_8_out, not_9_out;

  not not_1 (not_1_out, interrupt);
  not not_2 (not_2_out, OP[4]);
  not not_3 (not_3_out, OP[3]);
  not not_4 (not_4_out, OP[2]);
  not not_5 (not_5_out, OP[1]);
  not not_6 (not_6_out, OP[0]);
  not not_7 (not_7_out, SBC[2]);
  not not_8 (not_8_out, SBC[1]);
  not not_9 (not_9_out, SBC[0]);
  and and_1 (and_1_out, SBC[2], SBC[1], not_9_out);
  and and_2 (and_2_out, not_1_out, not_3_out, not_4_out, OP[1], not_6_out, SBC[1], SBC[0]);
  and and_3 (and_3_out, not_1_out, not_2_out, not_3_out, not_4_out, OP[1], OP[0], SBC[1]);
  and and_4 (and_4_out, not_1_out, not_3_out, OP[2], not_5_out, not_6_out, SBC[1], not_9_out);
  and and_5 (and_5_out, not_1_out, not_4_out, SBC[2]);
  and and_6 (and_6_out, not_1_out, not_8_out, SBC[0]);
  and and_7 (and_7_out, not_1_out, not_3_out, not_4_out, OP[1], not_6_out, SBC[0]);
  and and_8 (and_8_out, not_1_out, not_2_out, not_3_out, not_4_out, OP[1], OP[0], SBC[1]);
  and and_9 (and_9_out, not_1_out, not_3_out, OP[2], not_5_out, not_6_out, SBC[1], not_9_out);
  and and_10 (and_10_out, not_1_out, not_4_out, SBC[2]);
  and and_11 (and_11_out, not_7_out, not_8_out, not_9_out);
  and and_12 (and_12_out, not_1_out, not_3_out, not_4_out, OP[1], OP[0], SBC[1], SBC[0]);
  and and_13 (and_13_out, not_1_out, not_2_out, SBC[1], SBC[0]);
  and and_14 (and_14_out, not_1_out, not_2_out, not_3_out, not_4_out, not_5_out, not_9_out);
  and and_15 (and_15_out, not_1_out, not_2_out, not_3_out, not_4_out, not_6_out, not_9_out);
  and and_16 (and_16_out, not_1_out, not_2_out, not_4_out, OP[1], not_6_out, not_9_out);
  and and_17 (and_17_out, not_1_out, not_2_out, OP[3], not_4_out, OP[1], not_9_out);
  and and_18 (and_18_out, not_1_out, not_2_out, OP[3], OP[2], not_6_out, not_9_out);
  and and_19 (and_19_out, not_1_out, not_2_out, not_3_out, OP[2], OP[1], OP[0], not_9_out);
  and and_20 (and_20_out, not_1_out, not_3_out, not_4_out, not_5_out, OP[0], SBC[1], SBC[0]);
  and and_21 (and_21_out, interrupt, not_8_out, not_9_out);
  and and_22 (and_22_out, not_1_out, not_2_out, OP[3], not_4_out, OP[1], not_6_out, SBC[1]);
  and and_23 (and_23_out, not_1_out, not_2_out, SBC[1], SBC[0]);
  and and_24 (and_24_out, not_1_out, not_2_out, not_3_out, not_4_out, not_5_out, OP[0], SBC[1]);
  and and_25 (and_25_out, not_1_out, not_2_out, not_3_out, OP[2], OP[1], OP[0], SBC[1]);
  and and_26 (and_26_out, not_1_out, not_2_out, OP[3], not_4_out, SBC[1]);
  and and_27 (and_27_out, not_1_out, not_2_out, OP[3], not_5_out, OP[0], SBC[1]);
  and and_28 (and_28_out, not_1_out, not_2_out, not_3_out, OP[2], OP[1], not_6_out, SBC[1], not_9_out);
  and and_29 (and_29_out, not_1_out, not_2_out, not_3_out, not_4_out, OP[1], OP[0], SBC[1]);
  and and_30 (and_30_out, not_1_out, not_2_out, not_3_out, OP[2], not_5_out, OP[0], SBC[1], not_9_out);
  and and_31 (and_31_out, not_1_out, not_2_out, OP[3], not_4_out, not_5_out, OP[0], SBC[1]);
  and and_32 (and_32_out, not_1_out, not_2_out, not_3_out, not_4_out, OP[1], not_6_out, SBC[1]);
  and and_33 (and_33_out, not_1_out, not_2_out, not_3_out, not_4_out, not_5_out, OP[0], SBC[1]);
  and and_34 (and_34_out, interrupt, not_7_out, not_9_out);
  and and_35 (and_35_out, interrupt, not_8_out, not_9_out);
  and and_36 (and_36_out, not_1_out, OP[4], not_3_out, not_4_out, not_5_out, OP[0], SBC[1]);
  and and_37 (and_37_out, OP[4], not_3_out, not_4_out, OP[0], not_7_out, SBC[1], not_9_out);
  and and_38 (and_38_out, not_2_out, OP[3], not_4_out, not_5_out, not_7_out, SBC[1], not_9_out);
  and and_39 (and_39_out, not_2_out, OP[3], not_5_out, OP[0], not_7_out, SBC[1], not_9_out);
  and and_40 (and_40_out, SBC[2], not_8_out, SBC[0]);
  and and_41 (and_41_out, not_7_out, not_8_out, not_9_out);
  and and_42 (and_42_out, not_1_out, not_3_out, not_4_out, OP[1], not_6_out, not_9_out);
  and and_43 (and_43_out, not_1_out, not_3_out, OP[2], not_5_out, not_6_out, SBC[1], SBC[0]);
  and and_44 (and_44_out, not_1_out, not_2_out, OP[3], OP[1], SBC[1]);
  and and_45 (and_45_out, not_1_out, not_2_out, OP[2], OP[1], SBC[1]);
  and and_46 (and_46_out, not_1_out, not_2_out, not_3_out, not_5_out, OP[0], SBC[1]);
  and and_47 (and_47_out, not_1_out, not_2_out, not_3_out, not_4_out, not_5_out, not_9_out);
  and and_48 (and_48_out, not_1_out, not_2_out, OP[3], OP[2], not_6_out, not_9_out);
  and and_49 (and_49_out, not_1_out, not_8_out, SBC[0]);
  and and_50 (and_50_out, not_1_out, not_3_out, not_4_out, OP[1], not_6_out, SBC[0]);
  and and_51 (and_51_out, not_1_out, not_2_out, SBC[0]);
  and and_52 (and_52_out, not_1_out, not_6_out, SBC[2]);
  and and_53 (IRI, not_1_out, not_8_out, SBC[0]);
  and and_54 (IRO, not_1_out, not_2_out, not_3_out, OP[2], OP[1], OP[0], SBC[1]);
  and and_55 (and_55_out, not_1_out, not_2_out, not_3_out, OP[2], not_5_out, not_6_out, SBC[1]);
  and and_56 (and_56_out, not_1_out, not_2_out, OP[3], not_4_out, not_5_out, not_6_out, SBC[1]);
  and and_57 (and_57_out, not_1_out, not_4_out, not_5_out, SBC[2]);
  and and_58 (MOA, SBC[2], SBC[1], not_9_out);
  and and_59 (FDI, not_1_out, not_6_out, SBC[2]);
  and and_60 (OEn, not_1_out, not_2_out, OP[3], not_4_out, OP[1], OP[0], SBC[1]);
  and and_61 (and_61_out, interrupt, not_7_out, not_9_out);
  and and_62 (and_62_out, OP[4], not_3_out, not_4_out, OP[0], not_7_out, SBC[1], not_9_out);
  and and_63 (and_63_out, not_1_out, not_2_out, OP[3], OP[2], OP[1], not_6_out, SBC[1]);
  and and_64 (and_64_out, not_1_out, not_3_out, not_4_out, OP[1], not_6_out, SBC[1], SBC[0]);
  and and_65 (and_65_out, interrupt, not_7_out, SBC[0]);
  and and_66 (and_66_out, not_1_out, OP[4], not_3_out, not_4_out, OP[0], SBC[1], not_9_out);
  and and_67 (and_67_out, not_1_out, not_2_out, OP[3], OP[2], not_5_out, OP[0], SBC[1]);
  and and_68 (and_68_out, not_3_out, not_4_out, not_5_out, OP[0], not_7_out, SBC[1], SBC[0]);
  and and_69 (and_69_out, interrupt, not_7_out, not_9_out);
  and and_70 (and_70_out, interrupt, not_8_out, not_9_out);
  and and_71 (and_71_out, not_1_out, not_3_out, OP[2], not_5_out, not_6_out, SBC[1], SBC[0]);
  and and_72 (and_72_out, not_1_out, OP[4], not_3_out, not_4_out, not_5_out, OP[0], SBC[1]);
  and and_73 (and_73_out, OP[4], not_3_out, not_4_out, OP[1], not_6_out, not_7_out, SBC[1], not_9_out);
  and and_74 (and_74_out, not_2_out, OP[3], OP[2], OP[0], not_7_out, SBC[1], not_9_out);
  and and_75 (ICAO, SBC[2], not_8_out, SBC[0]);
  and and_76 (Prev0, not_1_out, not_3_out, OP[2], not_5_out, not_6_out, SBC[1], SBC[0]);
  and and_77 (Prev1, not_1_out, not_3_out, not_4_out, OP[1], OP[0], SBC[1], SBC[0]);
  and and_78 (SCJAO, not_1_out, OP[1], SBC[2]);
  and and_79 (RetIRI, not_1_out, not_3_out, not_4_out, OP[1], OP[0], SBC[1], SBC[0]);
  and and_80 (RetIRO, not_1_out, OP[4], not_3_out, OP[2], not_5_out, not_6_out, SBC[1], not_9_out);
  and and_81 (and_81_out, not_1_out, OP[4], not_4_out, not_5_out, not_6_out, SBC[1], not_9_out);
  and and_82 (and_82_out, not_1_out, OP[4], OP[2], OP[1], SBC[1], not_9_out);
  and and_83 (and_83_out, not_1_out, OP[4], OP[3], SBC[1], not_9_out);
  and and_84 (and_84_out, not_1_out, OP[4], OP[2], OP[0], SBC[1], not_9_out);
  and and_85 (and_85_out, not_1_out, not_2_out, OP[3], OP[2], not_6_out, SBC[1]);
  and and_86 (and_86_out, not_1_out, not_2_out, SBC[1], SBC[0]);
  and and_87 (and_87_out, not_1_out, not_2_out, not_3_out, not_4_out, not_5_out, SBC[1]);
  and and_88 (and_88_out, not_1_out, not_2_out, not_3_out, OP[2], OP[1], OP[0], SBC[1]);
  and and_89 (and_89_out, not_1_out, not_2_out, OP[3], not_4_out, OP[1], SBC[1]);
  and and_90 (and_90_out, not_1_out, not_2_out, not_3_out, not_4_out, not_6_out, SBC[1]);
  and and_91 (and_91_out, not_1_out, not_4_out, not_6_out, SBC[1], SBC[0]);
  and and_92 (and_92_out, SBC[2], SBC[1], SBC[0]);
  and and_93 (and_93_out, not_1_out, not_2_out, not_3_out, not_4_out, OP[1], OP[0], SBC[1]);
  and and_94 (and_94_out, not_1_out, not_2_out, not_3_out, OP[2], not_5_out, not_6_out, SBC[1]);
  and and_95 (and_95_out, not_1_out, OP[4], OP[2], OP[0], SBC[1], SBC[0]);
  and and_96 (and_96_out, not_1_out, not_2_out, OP[3], not_4_out, not_5_out, SBC[1]);
  and and_97 (and_97_out, not_1_out, not_2_out, OP[3], not_5_out, OP[0], SBC[1]);
  and and_98 (and_98_out, not_1_out, OP[4], OP[3], SBC[1], SBC[0]);
  and and_99 (and_99_out, not_1_out, not_4_out, SBC[2]);
  and and_100 (and_100_out, not_1_out, OP[4], OP[1], not_6_out, SBC[1], SBC[0]);
  and and_101 (RIR, SBC[2], SBC[1], SBC[0]);
  or or_1 (JMP, and_1_out, and_2_out, and_3_out, and_4_out, and_5_out);
  or or_2 (PCU, and_6_out, and_7_out, and_8_out, and_9_out, and_10_out);
  or or_3 (PCO, and_11_out, and_12_out, and_13_out, and_14_out, and_15_out, and_16_out, and_17_out, and_18_out, and_19_out);
  or or_4 (PCDBO, and_20_out, and_21_out);
  or or_5 (DRW, and_22_out, and_23_out, and_24_out, and_25_out);
  or or_6 (SR1O, and_26_out, and_27_out);
  or or_7 (SR2O, and_28_out, and_29_out, and_30_out, and_31_out);
  or or_8 (ALUCalc, and_32_out, and_33_out);
  or or_9 (MI, and_34_out, and_35_out, and_36_out, and_37_out, and_38_out, and_39_out);
  or or_10 (ML, and_40_out, and_41_out, and_42_out, and_43_out, and_44_out, and_45_out, and_46_out, and_47_out, and_48_out);
  or or_11 (MO, and_49_out, and_50_out, and_51_out, and_52_out);
  or or_12 (IRAO, and_55_out, and_56_out, and_57_out);
  or or_13 (FRO, and_61_out, and_62_out);
  or or_14 (SPInc, and_63_out, and_64_out);
  or or_15 (SPDec, and_65_out, and_66_out, and_67_out, and_68_out);
  or or_16 (SPO, and_69_out, and_70_out, and_71_out, and_72_out, and_73_out, and_74_out);
  or or_17 (HLT, and_81_out, and_82_out, and_83_out, and_84_out);
  or or_18 (JSC1, and_85_out, and_86_out, and_87_out, and_88_out, and_89_out, and_90_out);
  or or_19 (RSC, and_91_out, and_92_out, and_93_out, and_94_out, and_95_out, and_96_out, and_97_out, and_98_out, and_99_out, and_100_out);

  assign SPI = 1'b0;
endmodule

module vgaCard (
  input  R,
  input  En,
  input  clock,
  input  nig,
  output [9:0] H,
  output [9:0] V,
  output pic,
  output [18:0] pxCod,
  output HS,
  output VS
);

  wire or_1_out, vgatimig_1_pic, vgatimig_1_pulse, vgatimig_2_nxt, vgatimig_2_pic;
  wire [11:0] vgatimig_1_cod, vgatimig_2_cod;

  vgaTimig vgatimig_1 (
    .R(R), .En(En), .clock(clock), .resolution(12'h280), .BP(12'h10), .sync(12'h60), .FP(12'h30), .nig(nig),
    .cod(vgatimig_1_cod), .pic(vgatimig_1_pic), .nxt(HS), .pulse(vgatimig_1_pulse));
  vgaTimig vgatimig_2 (
    .R(R), .En(En), .clock(vgatimig_1_pulse), .resolution(12'h1e0), .BP(12'ha), .sync(12'h2), .FP(12'h21),
    .nig(nig), .cod(vgatimig_2_cod), .pic(vgatimig_2_pic), .nxt(vgatimig_2_nxt), .pulse(VS));
  and and_1 (pic, vgatimig_2_pic, vgatimig_1_pic);
  Bit_Extender #(.in_width(12), .out_width(10)) bit_extender_1 (.in(vgatimig_1_cod), .out(H));
  Bit_Extender #(.in_width(12), .out_width(10)) bit_extender_2 (.in(vgatimig_2_cod), .out(V));
  Counter #(.max('h4b000), .width(19)) counter_1 (
    .clr(or_1_out), .load(1'b0), .up(1'b1), .count(pic), .clk(clock), .Q(pxCod));  // open: D, carry
  or or_1 (or_1_out, R, vgatimig_2_nxt);
endmodule

module vgaTimig (
  input  R,
  input  En,
  input  clock,
  input  [11:0] resolution,
  input  [11:0] BP,
  input  [11:0] sync,
  input  [11:0] FP,
  input  nig,
  output [11:0] cod,
  output pic,
  output nxt,
  output pulse
);

  wire and_2_out, comparator_1_eq, comparator_2_eq, comparator_3_eq, d_ff_1_q, or_1_out;
  wire [11:0] subtractor_1_out, subtractor_2_out, subtractor_3_out, subtractor_4_out;

  Subtractor #(.width(12)) subtractor_1 (.a(resolution), .b(12'h1), .out(subtractor_1_out));  // open: bin, bout
  Subtractor #(.width(12)) subtractor_2 (.a({12{1'b0}}), .b(BP), .out(subtractor_2_out));  // open: bin, bout
  Subtractor #(.width(12)) subtractor_3 (.a(subtractor_2_out), .b(sync), .out(subtractor_3_out));  // open: bin, bout
  Subtractor #(.width(12)) subtractor_4 (.a(subtractor_3_out), .b(FP), .out(subtractor_4_out));  // open: bin, bout
  Comparator #(.mode("unsigned"), .width(12)) comparator_1 (
    .a(cod), .b(subtractor_1_out), .eq(comparator_1_eq));  // open: gt, lt
  Comparator #(.mode("unsigned"), .width(12)) comparator_2 (
    .a(cod), .b(subtractor_2_out), .eq(comparator_2_eq));  // open: gt, lt
  Comparator #(.mode("unsigned"), .width(12)) comparator_3 (
    .a(cod), .b(subtractor_3_out), .eq(comparator_3_eq));  // open: gt, lt
  or or_1 (or_1_out, comparator_3_eq, d_ff_1_q);
  and and_1 (nxt, En, comparator_1_eq);
  and and_2 (and_2_out, ~comparator_2_eq, or_1_out);  // AND_Gate
  D_Flip_Flop d_ff_1 (.D(and_2_out), .clk(clock), .Q(d_ff_1_q), .reset(R));  // open: Qn, preset
  Counter #(.max('hfff), .width(12)) counter_1 (
    .clr(R), .load(nxt), .up(1'b1), .count(En), .clk(clock), .D(subtractor_4_out), .Q(cod));  // open: carry
  xor xor_1 (pulse, d_ff_1_q, nig);
  Comparator #(.mode("unsigned"), .width(12)) comparator_4 (.a(cod), .b(resolution), .lt(pic));  // open: gt, eq
endmodule

module VMCU (
  input  R,
  input  VCC,
  input  [18:0] VDA,
  input  [18:0] SDA,
  input  W,
  input  [23:0] SD,
  input  RC,
  output busy,
  output [23:0] VDO
);

  wire d_ff_1_qn;
  wire [19:0] bit_extender_1_out, bit_extender_2_out, multiplexer_1_out;
  wire [23:0] VRAM_dout;

  D_Flip_Flop d_ff_1 (.D(VCC), .clk(RC), .Qn(d_ff_1_qn), .reset(R));  // open: Q, preset
  and and_1 (busy, VCC, d_ff_1_qn);
  assign bit_extender_1_out = {{1{1'b0}}, VDA};  // Bit_Extender bit_extender_1
  assign bit_extender_2_out = {{1{1'b0}}, SDA};  // Bit_Extender bit_extender_2
  Multiplexer #(.width(20)) multiplexer_1 (
    .in0(bit_extender_2_out), .in1(bit_extender_1_out), .out(multiplexer_1_out), .sel(busy));
  RAM #(.addrWidth(20), .dataWidth(24), .enables("line")) VRAM (
    .addr(multiplexer_1_out), .we(W), .clk(RC), .din(SD), .dout(VRAM_dout));
  Register #(.width(24)) register_1 (.D(VRAM_dout), .en(busy), .clk(RC), .Q(VDO), .clr(R));
endmodule

module MCMU (
  input  [23:0] adr,
  input  VCMB,
  input  W,
  input  Rd,
  input  privilege,
  input  Clock,
  input  R,
  output [23:0] Adress,
  output stall,
  output VCMW,
  output RW,
  output RL
);

  wire and_1_out, and_2_out, and_3_out, and_4_out, comparator_1_lt, comparator_2_gt, d_ff_1_qn, d_ff_2_qn;
  wire [14:0] bit_extender_1_out;
  wire [16:0] ram_1_dout;

  RAM #(.addrWidth(15), .dataWidth(17), .enables("line"), .trigger("falling")) ram_1 (
    .addr(adr[23:9]), .clk(Clock), .dout(ram_1_dout));  // open: we, din
  Bit_Extender #(.in_width(17), .out_width(15), .\type ("zero")) bit_extender_1 (
    .in(ram_1_dout), .out(bit_extender_1_out));
  Multiplexer #(.width(24)) multiplexer_1 (
    .in0({bit_extender_1_out, adr[8:0]}), .in1(adr), .out(Adress), .sel(privilege));
  Comparator #(.mode("unsigned"), .width(24)) comparator_1 (
    .a(Adress), .b(24'hfff000), .lt(comparator_1_lt));  // open: gt, eq
  Comparator #(.mode("unsigned"), .width(24)) comparator_2 (
    .a(Adress), .b(24'hfb4000), .gt(comparator_2_gt));  // open: eq, lt
  and and_1 (and_1_out, comparator_1_lt, comparator_2_gt);
  and and_2 (and_2_out, and_1_out, W);
  and and_3 (and_3_out, ~and_1_out, W);  // AND_Gate
  and and_4 (and_4_out, ~and_1_out, Rd);  // AND_Gate
  D_Flip_Flop d_ff_1 (.D(and_3_out), .clk(Clock), .Qn(d_ff_1_qn), .reset(R));  // open: Q, preset
  D_Flip_Flop d_ff_2 (.D(and_4_out), .clk(Clock), .Qn(d_ff_2_qn), .reset(R));  // open: Q, preset
  and and_5 (stall, and_2_out, VCMB);
  and and_6 (VCMW, and_2_out, ~VCMB);  // AND_Gate
  and and_7 (RW, and_3_out, d_ff_1_qn);
  and and_8 (RL, and_4_out, d_ff_2_qn);

  // Other names for the same wires on the sheet: C = Clock; Ld = Rd; PVG = privilege
endmodule

module InstrDcdL2 (
  input  [3:0] opI,
  input  JF,
  input  [1:0] SOT,
  output [4:0] OP
);

  wire and_1_out, and_2_out, and_3_out, and_4_out, and_5_out, and_6_out, and_7_out, and_8_out, and_9_out,
       and_10_out, and_11_out, and_12_out, and_13_out, and_14_out, and_15_out, and_16_out, and_17_out,
       and_18_out, and_19_out, and_20_out, and_21_out, and_22_out, and_23_out, and_24_out, and_25_out,
       and_26_out, and_27_out, and_28_out, and_29_out, and_30_out, and_31_out, and_32_out, not_1_out,
       not_2_out, not_3_out, not_4_out, not_5_out, not_6_out, not_7_out;

  not not_1 (not_1_out, opI[3]);
  not not_2 (not_2_out, opI[2]);
  not not_3 (not_3_out, opI[1]);
  not not_4 (not_4_out, opI[0]);
  not not_5 (not_5_out, JF);
  not not_6 (not_6_out, SOT[1]);
  not not_7 (not_7_out, SOT[0]);
  and and_1 (and_1_out, opI[3], opI[2], SOT[1], SOT[0]);
  and and_2 (and_2_out, opI[3], opI[2], opI[0]);
  and and_3 (and_3_out, opI[3], opI[2], opI[1]);
  and and_4 (and_4_out, opI[3], not_2_out);
  and and_5 (and_5_out, opI[3], not_3_out, not_4_out, not_6_out);
  and and_6 (and_6_out, opI[3], not_3_out, not_4_out, not_7_out);
  and and_7 (and_7_out, not_1_out, opI[2], opI[1], opI[0]);
  and and_8 (and_8_out, not_2_out, opI[1], opI[0], JF);
  and and_9 (and_9_out, not_1_out, opI[2], not_3_out);
  and and_10 (and_10_out, not_1_out, opI[2], not_4_out);
  and and_11 (and_11_out, opI[3], opI[1], opI[0]);
  and and_12 (and_12_out, opI[2], not_3_out, not_4_out, not_6_out);
  and and_13 (and_13_out, opI[2], not_3_out, not_4_out, not_7_out);
  and and_14 (and_14_out, opI[2], opI[1], not_4_out, JF);
  and and_15 (and_15_out, not_1_out, not_2_out, opI[1], not_5_out);
  and and_16 (and_16_out, not_1_out, opI[2], not_3_out, opI[0]);
  and and_17 (and_17_out, not_1_out, opI[1], not_4_out);
  and and_18 (and_18_out, opI[3], not_2_out, not_3_out, opI[0]);
  and and_19 (and_19_out, not_2_out, opI[1], not_4_out);
  and and_20 (and_20_out, opI[3], opI[2], not_3_out, not_4_out, not_6_out, SOT[0]);
  and and_21 (and_21_out, opI[3], opI[2], not_3_out, SOT[1], not_7_out);
  and and_22 (and_22_out, opI[1], not_4_out, not_5_out);
  and and_23 (and_23_out, opI[3], not_3_out, opI[0], SOT[1]);
  and and_24 (and_24_out, not_1_out, not_2_out, not_3_out, opI[0]);
  and and_25 (and_25_out, not_1_out, not_2_out, opI[0], not_5_out);
  and and_26 (and_26_out, not_1_out, opI[2], not_4_out);
  and and_27 (and_27_out, opI[3], not_2_out, not_4_out);
  and and_28 (and_28_out, opI[3], opI[2], opI[0], not_6_out);
  and and_29 (and_29_out, opI[3], opI[2], opI[1], opI[0]);
  and and_30 (and_30_out, opI[2], not_3_out, not_4_out, not_7_out);
  and and_31 (and_31_out, opI[2], not_4_out, not_5_out, not_7_out);
  and and_32 (and_32_out, opI[3], opI[1], not_4_out, not_5_out);
  or or_1 (OP[4], and_1_out, and_2_out, and_3_out);
  or or_2 (OP[3], and_4_out, and_5_out, and_6_out, and_7_out);
  or or_3 (OP[2], and_8_out, and_9_out, and_10_out, and_11_out, and_12_out, and_13_out, and_14_out);
  or or_4 (OP[1], and_15_out, and_16_out, and_17_out, and_18_out, and_19_out, and_20_out, and_21_out, and_22_out, and_23_out);
  or or_5 (OP[0], and_24_out, and_25_out, and_26_out, and_27_out, and_28_out, and_29_out, and_30_out, and_31_out, and_32_out);
endmodule

module andClock (
  input  C,
  input  S,
  output O
);

  and and_1 (O, C, S);
endmodule

module InteruptSR (
  input  R,
  input  St,
  input  C,
  output stall,
  output clrIB,
  output IntConstO,
  output ML,
  output MO,
  output jmp,
  output MI,
  output SPD,
  output SPO,
  output PCDBO
);

  wire or_1_out;
  wire [2:0] counter_1_q;

  or or_1 (or_1_out, clrIB, R);
  Counter #(.max('h7), .width(3)) counter_1 (
    .clr(or_1_out), .load(1'b0), .up(1'b1), .count(St), .clk(C), .Q(counter_1_q));  // open: D, carry
  InteruptSRCA interuptsrca_1 (
    .en(St), .counter(counter_1_q), .stall(stall), .clrIB(clrIB), .ImtConst(IntConstO), .ML(ML), .MO(MO),
    .jmp(jmp), .MI(MI), .SPD(SPD), .SPO(SPO), .PCDBO(PCDBO));
endmodule

module InteruptSRCA (
  input  en,
  input  [2:0] counter,
  output stall,
  output clrIB,
  output ImtConst,
  output ML,
  output MO,
  output jmp,
  output MI,
  output SPD,
  output SPO,
  output PCDBO
);

  wire not_1_out, not_2_out, not_3_out;

  not not_1 (not_1_out, counter[2]);
  not not_2 (not_2_out, counter[1]);
  not not_3 (not_3_out, counter[0]);
  and and_1 (stall, en, not_1_out);
  and and_2 (clrIB, en, counter[2], not_2_out, not_3_out);
  and and_3 (ImtConst, en, not_1_out, counter[1], not_3_out);
  and and_4 (ML, en, not_1_out, counter[1], not_3_out);
  and and_5 (MO, en, not_1_out, counter[1], counter[0]);
  and and_6 (jmp, en, not_1_out, counter[1], counter[0]);
  and and_7 (MI, en, not_1_out, not_2_out, counter[0]);
  and and_8 (SPD, en, not_1_out, not_2_out, not_3_out);
  and and_9 (SPO, en, not_1_out, not_2_out, counter[0]);
  and and_10 (PCDBO, en, not_1_out, not_2_out, counter[0]);
endmodule

module Interuptr (
  input  KBAvb,
  input  [6:0] KBChar,
  output interupt,
  output [1:0] InteruptDevID,
  output [31:0] data
);

  assign data = {{25{1'b0}}, KBChar};  // Bit_Extender bit_extender_1

  assign interupt = KBAvb;
  assign InteruptDevID = 2'b01;
endmodule

module dspCNT (
  input  [9:0] x_cod,
  input  [9:0] y_cod,
  output d1_1,
  output d1_2,
  output d1_3,
  output d2_1,
  output d2_2,
  output d2_3
);

  wire and_1_out, and_2_out, and_3_out, and_4_out, and_5_out, comparator_1_eq, comparator_1_gt,
       comparator_2_eq, comparator_2_gt, comparator_3_eq, comparator_3_gt, comparator_4_eq, comparator_4_gt,
       comparator_5_eq, comparator_5_gt, not_1_out, not_2_out, not_3_out, not_4_out, not_5_out, or_1_out,
       or_2_out, or_3_out, or_4_out, or_5_out;

  Comparator #(.mode("unsigned"), .width(10)) comparator_1 (
    .a(x_cod), .b(10'h100), .gt(comparator_1_gt), .eq(comparator_1_eq));  // open: lt
  Comparator #(.mode("unsigned"), .width(10)) comparator_2 (
    .a(x_cod), .b(10'h200), .gt(comparator_2_gt), .eq(comparator_2_eq));  // open: lt
  Comparator #(.mode("unsigned"), .width(10)) comparator_3 (
    .a(x_cod), .b(10'h300), .gt(comparator_3_gt), .eq(comparator_3_eq));  // open: lt
  or or_1 (or_1_out, comparator_1_gt, comparator_1_eq);
  or or_2 (or_2_out, comparator_2_gt, comparator_2_eq);
  or or_3 (or_3_out, comparator_3_gt, comparator_3_eq);
  or or_4 (or_4_out, comparator_4_gt, comparator_4_eq);
  Comparator #(.mode("unsigned"), .width(10)) comparator_4 (
    .a(y_cod), .b(10'h100), .gt(comparator_4_gt), .eq(comparator_4_eq));  // open: lt
  or or_5 (or_5_out, comparator_5_gt, comparator_5_eq);
  Comparator #(.mode("unsigned"), .width(10)) comparator_5 (
    .a(y_cod), .b(10'h200), .gt(comparator_5_gt), .eq(comparator_5_eq));  // open: lt
  not not_1 (not_1_out, or_1_out);
  not not_2 (not_2_out, or_2_out);
  not not_3 (not_3_out, or_3_out);
  not not_4 (not_4_out, or_4_out);
  not not_5 (not_5_out, or_5_out);
  and and_1 (and_1_out, not_1_out, not_2_out, not_3_out);
  and and_2 (and_2_out, or_1_out, not_2_out, not_3_out);
  and and_3 (and_3_out, or_2_out, not_3_out);
  and and_4 (and_4_out, not_4_out, not_5_out);
  and and_5 (and_5_out, or_4_out, not_5_out);
  and and_6 (d1_1, and_1_out, and_4_out);
  and and_7 (d1_2, and_2_out, and_4_out);
  and and_8 (d1_3, and_3_out, and_4_out);
  and and_9 (d2_1, and_1_out, and_5_out);
  and and_10 (d2_2, and_2_out, and_5_out);
  and and_11 (d2_3, and_3_out, and_5_out);
endmodule

module tmpCA (
  input  OD,
  input  Prev0,
  input  Prev1,
  output Data
);

  wire and_1_out;

  and and_1 (and_1_out, OD, ~Prev0);  // AND_Gate
  or or_1 (Data, and_1_out, Prev1);
endmodule
